// Logisim project riscv.circ as structural Verilog: 22 circuits, main circuit main
module main (
  input  [31:0] read_value,
  input  [31:0] instruction,
  input  reset,
  output error,
  output [31:0] address,
  output [31:0] write_value,
  output read,
  output [31:0] pc_out,
  output [3:0] mask
);

  wire alu_1_neg, alu_1_zero, and_1_out, and_2_out, and_3_out, and_4_out, and_5_out, and_6_out, and_7_out,
       and_8_out, and_9_out, and_10_out, and_11_out, and_12_out, and_13_out, and_14_out, and_15_out,
       and_16_out, and_17_out, and_18_out, and_19_out, and_20_out, and_21_out, comp_1_true, not_1_out,
       not_2_out, not_3_out, not_4_out, not_5_out, not_6_out, not_7_out, not_8_out, not_9_out, not_10_out,
       not_11_out, not_12_out, not_13_out, not_14_out, not_15_out, not_16_out, not_17_out, op_to_alu_1_error,
       op_to_alu_1_out_15, op_to_alu_1_out_16, op_to_alu_1_out_17, op_to_alu_1_out_18, op_to_alu_1_out_19,
       op_to_alu_1_out_20, opcode_1_error, opcode_1_out_3, opcode_1_out_4, opcode_1_out_5, opcode_1_out_6,
       opcode_1_out_7, opcode_1_out_8, opcode_1_out_9, opcode_1_out_10, opcode_1_out_11, opcode_1_out_12,
       opcode_1_out_13, or_2_out, or_3_out, or_4_out, or_5_out, or_6_out, or_7_out, or_8_out, or_9_out,
       or_10_out, or_11_out, or_12_out, or_13_out, or_14_out, or_15_out, or_16_out, or_17_out, or_18_out,
       or_19_out, or_20_out, or_21_out, or_22_out, or_23_out, or_24_out, or_25_out, or_26_out, or_27_out,
       or_28_out, or_29_out, or_30_out, or_31_out, or_32_out;
  wire [31:0] add_er_1_result, alu_1_result, imm_1_result, mux32_1_out_4, mux32_2_out_4, mux32_3_out_4,
       mux32_4_out_4, mux32_5_out_4, mux32_6_out_4, mux32_7_out_4, mux32_8_out_4, pc_1_out_5,
       select_register_1_out1, select_register_1_out2, sign_1_result;

  Clock clock_1 ();  // open: out
  and and_1 (and_1_out, instruction[12], instruction[13]);
  or or_1 (error, or_2_out, and_2_out);
  or or_2 (or_2_out, opcode_1_error, op_to_alu_1_error);
  opcode opcode_1 (
    .op(instruction[6:0]), .error(opcode_1_error), .out_3(opcode_1_out_3), .out_4(opcode_1_out_4),
    .out_5(opcode_1_out_5), .out_6(opcode_1_out_6), .out_7(opcode_1_out_7), .out_8(opcode_1_out_8),
    .out_9(opcode_1_out_9), .out_10(opcode_1_out_10), .out_11(opcode_1_out_11), .out_12(opcode_1_out_12),
    .out_13(opcode_1_out_13));
  or or_3 (or_3_out, opcode_1_out_13, opcode_1_out_12);
  not not_1 (not_1_out, instruction[13]);
  not not_2 (not_2_out, instruction[12]);
  not not_3 (not_3_out, instruction[13]);
  not not_4 (not_4_out, instruction[12]);
  and and_2 (and_2_out, and_1_out, or_4_out);
  or or_4 (or_4_out, opcode_1_out_3, opcode_1_out_4);
  and and_3 (and_3_out, opcode_1_out_3, not_5_out);
  not not_5 (not_5_out, opcode_1_out_4);
  or or_5 (or_5_out, opcode_1_out_11, opcode_1_out_6);
  or or_6 (or_6_out, or_3_out, or_5_out);
  or or_7 (or_7_out, or_6_out, opcode_1_out_3);
  imm imm_1 (
    .in_6(instruction[11:7]), .in_7(instruction[14:12]), .in_8(instruction[19:15]),
    .in_9(instruction[24:20]), .in_10(instruction[31:25]), .I(or_7_out), .S(opcode_1_out_4),
    .B(opcode_1_out_7), .U(or_9_out), .J(opcode_1_out_10), .result(imm_1_result));
  and and_4 (and_4_out, not_1_out, not_2_out);
  and and_5 (and_5_out, not_3_out, instruction[12]);
  and and_6 (and_6_out, instruction[13], not_4_out);
  not not_6 (not_6_out, error);
  not not_7 (not_7_out, or_4_out);
  or or_8 (or_8_out, opcode_1_out_10, opcode_1_out_9);
  or or_9 (or_9_out, opcode_1_out_9, opcode_1_out_8);
  sign sign_1 (.unsign(instruction[14]), .read(mask), .value(read_value), .result(sign_1_result));
  not not_8 (not_8_out, or_17_out);
  and and_7 (and_7_out, not_6_out, not_8_out);
  or or_10 (or_10_out, opcode_1_out_5, opcode_1_out_7);
  or or_11 (or_11_out, opcode_1_out_3, opcode_1_out_5);
  or or_12 (or_12_out, or_11_out, or_13_out);
  mux32 mux32_1 (.in_3(add_er_1_result), .in_2(alu_1_result), .in_1(opcode_1_out_10), .out_4(mux32_1_out_4));
  and and_8 (and_8_out, not_6_out, or_17_out);
  pc pc_1 (.load(and_8_out), .reset(reset), .inc(and_7_out), .in_4(mux32_8_out_4), .out_5(pc_1_out_5));
  or or_13 (or_13_out, opcode_1_out_6, opcode_1_out_8);
  or or_14 (or_14_out, opcode_1_out_11, opcode_1_out_10);
  or or_15 (or_15_out, or_14_out, opcode_1_out_9);
  or or_16 (or_16_out, or_12_out, or_15_out);
  mux32 mux32_2 (.in_3(sign_1_result), .in_2(mux32_1_out_4), .in_1(opcode_1_out_3), .out_4(mux32_2_out_4));
  or or_17 (or_17_out, and_9_out, or_14_out);
  or or_18 (or_18_out, opcode_1_out_5, opcode_1_out_4);
  or or_19 (or_19_out, opcode_1_out_3, opcode_1_out_11);
  or or_20 (or_20_out, or_18_out, or_19_out);
  or or_21 (or_21_out, opcode_1_out_7, or_18_out);
  or or_22 (or_22_out, or_20_out, or_23_out);
  select_register select_register_1 (
    .load2(or_21_out), .store(or_16_out), .load1(or_22_out), .rs2(instruction[24:20]),
    .rd(instruction[11:7]), .rs1(instruction[19:15]), .in1(mux32_2_out_4), .out1(select_register_1_out1),
    .out2(select_register_1_out2));
  and and_9 (and_9_out, opcode_1_out_7, comp_1_true);
  or or_23 (or_23_out, opcode_1_out_6, opcode_1_out_7);
  mux32 mux32_3 (.in_3(pc_1_out_5), .in_2(select_register_1_out1), .in_1(or_8_out), .out_4(mux32_3_out_4));
  mux32 mux32_4 (.in_3({32{1'b0}}), .in_2(mux32_3_out_4), .in_1(opcode_1_out_8), .out_4(mux32_4_out_4));
  mux32 mux32_5 (.in_3(select_register_1_out2), .in_2(imm_1_result), .in_1(or_10_out), .out_4(mux32_5_out_4));
  mux32 mux32_6 (.in_3(32'h4), .in_2(mux32_5_out_4), .in_1(opcode_1_out_10), .out_4(mux32_6_out_4));
  op_to_ALU op_to_alu_1 (
    .in_12(instruction[30]), .in_13(instruction[14:12]), .in_11(opcode_1_out_13), .in_2(opcode_1_out_4),
    .in_3(opcode_1_out_5), .in_4(opcode_1_out_6), .in_5(opcode_1_out_7), .in_6(opcode_1_out_8),
    .in_1(opcode_1_out_3), .in_7(opcode_1_out_9), .in_8(opcode_1_out_10), .in_9(opcode_1_out_11),
    .in_10(opcode_1_out_12), .error(op_to_alu_1_error), .out_17(op_to_alu_1_out_17),
    .out_18(op_to_alu_1_out_18), .out_19(op_to_alu_1_out_19), .out_20(op_to_alu_1_out_20),
    .out_15(op_to_alu_1_out_15), .out_16(op_to_alu_1_out_16));
  mux32 mux32_7 (.in_3(32'h4), .in_2(imm_1_result), .in_1(opcode_1_out_11), .out_4(mux32_7_out_4));
  ALU alu_1 (
    .b(mux32_6_out_4), .mode0(op_to_alu_1_out_15), .mode1(op_to_alu_1_out_16), .sub(op_to_alu_1_out_17),
    .arith(op_to_alu_1_out_18), .logic0(op_to_alu_1_out_19), .logic1(op_to_alu_1_out_20), .a(mux32_4_out_4),
    .result(alu_1_result), .neg(alu_1_neg), .zero(alu_1_zero));
  add_er add_er_1 (.A(pc_1_out_5), .B(mux32_7_out_4), .result(add_er_1_result));
  mux32 mux32_8 (.in_3(alu_1_result), .in_2(add_er_1_result), .in_1(opcode_1_out_11), .out_4(mux32_8_out_4));
  comp comp_1 (.f3(instruction[14:12]), .zero(alu_1_zero), .neg(alu_1_neg), .true(comp_1_true));
  not not_9 (not_9_out, alu_1_result[1]);
  not not_10 (not_10_out, alu_1_result[0]);
  and and_10 (and_10_out, not_10_out, not_11_out);
  not not_11 (not_11_out, alu_1_result[1]);
  and and_11 (and_11_out, alu_1_result[0], not_12_out);
  not not_12 (not_12_out, alu_1_result[1]);
  not not_13 (not_13_out, alu_1_result[0]);
  and and_12 (and_12_out, not_13_out, alu_1_result[1]);
  and and_13 (and_13_out, alu_1_result[0], alu_1_result[1]);
  and and_14 (and_14_out, and_10_out, and_4_out);
  and and_15 (and_15_out, not_9_out, and_5_out);
  and and_16 (and_16_out, and_11_out, and_4_out);
  and and_17 (and_17_out, not_9_out, and_5_out);
  and and_18 (and_18_out, and_12_out, and_4_out);
  not not_14 (not_14_out, not_9_out);
  and and_19 (and_19_out, not_14_out, and_5_out);
  and and_20 (and_20_out, and_13_out, and_4_out);
  not not_15 (not_15_out, not_9_out);
  and and_21 (and_21_out, not_15_out, and_5_out);
  or or_24 (or_24_out, and_14_out, and_15_out);
  or or_25 (or_25_out, and_16_out, and_17_out);
  or or_26 (or_26_out, and_18_out, and_19_out);
  or or_27 (or_27_out, and_20_out, and_21_out);
  not not_16 (not_16_out, or_32_out);
  or or_28 (or_28_out, or_24_out, and_6_out);
  or or_29 (or_29_out, or_25_out, and_6_out);
  or or_30 (or_30_out, or_26_out, and_6_out);
  or or_31 (or_31_out, or_27_out, and_6_out);
  or or_32 (or_32_out, error, not_7_out);
  and and_22 (mask[0], not_16_out, or_28_out);
  and and_23 (mask[1], not_16_out, or_29_out);
  and and_24 (mask[2], not_16_out, or_30_out);
  and and_25 (mask[3], not_16_out, or_31_out);
  mux32 mux32_9 (.in_3({32{1'b0}}), .in_2(alu_1_result), .in_1(or_32_out), .out_4(address));
  mux32 mux32_10 (.in_3({32{1'b0}}), .in_2(select_register_1_out2), .in_1(or_32_out), .out_4(write_value));
  not not_17 (not_17_out, error);
  and and_26 (read, not_17_out, and_3_out);
  mux32 mux32_11 (.in_3({32{1'b0}}), .in_2(pc_1_out_5), .in_1(error), .out_4(pc_out));

  // Notes on the sheet:
  //   input
  //   output
endmodule

module pc (
  input  reset,
  input  inc,
  input  load,
  input  [31:0] in_4,
  output [31:0] out_5
);

  wire and_1_out, and_2_out, and_3_out, and_4_out, and_5_out, and_6_out, and_7_out, and_8_out, and_9_out,
       and_10_out, and_11_out, and_12_out, and_13_out, and_14_out, and_15_out, and_16_out, and_17_out,
       and_18_out, and_19_out, and_20_out, and_21_out, and_22_out, and_23_out, and_24_out, and_25_out,
       and_26_out, and_27_out, and_28_out, and_29_out, and_30_out, and_31_out, and_32_out, and_33_out,
       and_34_out, and_35_out, and_36_out, and_37_out, and_38_out, and_39_out, and_40_out, and_41_out,
       and_42_out, and_43_out, and_44_out, and_45_out, and_46_out, and_47_out, and_48_out, and_49_out,
       and_50_out, and_51_out, and_52_out, and_53_out, and_54_out, and_55_out, and_56_out, and_57_out,
       and_58_out, and_59_out, and_60_out, and_61_out, and_62_out, and_63_out, and_64_out, and_65_out,
       and_66_out, and_67_out, and_68_out, and_69_out, and_70_out, and_71_out, and_72_out, and_73_out,
       and_74_out, and_75_out, and_76_out, and_77_out, and_78_out, and_79_out, and_80_out, and_81_out,
       and_82_out, and_83_out, and_84_out, and_85_out, and_86_out, and_87_out, and_88_out, and_89_out,
       and_90_out, and_91_out, and_92_out, and_93_out, and_94_out, and_95_out, and_96_out, and_97_out,
       and_98_out, and_99_out, and_100_out, and_101_out, and_102_out, and_103_out, and_104_out, and_105_out,
       and_106_out, and_107_out, and_108_out, and_109_out, and_110_out, and_111_out, and_112_out,
       and_113_out, and_114_out, and_115_out, and_116_out, and_117_out, and_118_out, and_119_out,
       and_120_out, and_121_out, and_122_out, and_123_out, and_124_out, and_125_out, and_126_out,
       and_127_out, and_128_out, and_129_out, and_130_out, dff_1_out_2, dff_2_out_2, dff_3_out_2,
       dff_4_out_2, dff_5_out_2, dff_6_out_2, dff_7_out_2, dff_8_out_2, dff_9_out_2, dff_10_out_2,
       dff_11_out_2, dff_12_out_2, dff_13_out_2, dff_14_out_2, dff_15_out_2, dff_16_out_2, dff_17_out_2,
       dff_18_out_2, dff_19_out_2, dff_20_out_2, dff_21_out_2, dff_22_out_2, dff_23_out_2, dff_24_out_2,
       dff_25_out_2, dff_26_out_2, dff_27_out_2, dff_28_out_2, dff_29_out_2, dff_30_out_2, dff_31_out_2,
       dff_32_out_2, not_1_out, not_2_out, or_1_out, or_2_out, or_3_out, or_4_out, or_5_out, or_6_out,
       or_7_out, or_8_out, or_9_out, or_10_out, or_11_out, or_12_out, or_13_out, or_14_out, or_15_out,
       or_16_out, or_17_out, or_18_out, or_19_out, or_20_out, or_21_out, or_22_out, or_23_out, or_24_out,
       or_25_out, or_26_out, or_27_out, or_28_out, or_29_out, or_30_out, or_31_out, or_32_out;

  not not_1 (not_1_out, reset);
  Clock clock_1 ();  // open: out
  not not_2 (not_2_out, load);
  and and_1 (and_1_out, not_1_out, load);
  and and_2 (and_2_out, not_1_out, inc);
  and and_3 (and_3_out, and_2_out, not_2_out);
  and and_4 (and_4_out, and_1_out, in_4[0]);
  and and_5 (and_5_out, not_2_out, and_68_out);
  and and_6 (and_6_out, and_1_out, in_4[1]);
  and and_7 (and_7_out, not_2_out, and_69_out);
  and and_8 (and_8_out, and_1_out, in_4[2]);
  and and_9 (and_9_out, not_2_out, and_70_out);
  and and_10 (and_10_out, and_1_out, in_4[3]);
  and and_11 (and_11_out, not_2_out, and_71_out);
  and and_12 (and_12_out, and_1_out, in_4[4]);
  and and_13 (and_13_out, not_2_out, and_72_out);
  and and_14 (and_14_out, and_1_out, in_4[5]);
  and and_15 (and_15_out, not_2_out, and_73_out);
  and and_16 (and_16_out, and_1_out, in_4[6]);
  and and_17 (and_17_out, not_2_out, and_74_out);
  and and_18 (and_18_out, and_1_out, in_4[7]);
  and and_19 (and_19_out, not_2_out, and_75_out);
  and and_20 (and_20_out, and_1_out, in_4[8]);
  and and_21 (and_21_out, not_2_out, and_76_out);
  and and_22 (and_22_out, and_1_out, in_4[9]);
  and and_23 (and_23_out, not_2_out, and_77_out);
  and and_24 (and_24_out, and_1_out, in_4[10]);
  and and_25 (and_25_out, not_2_out, and_78_out);
  and and_26 (and_26_out, and_1_out, in_4[11]);
  and and_27 (and_27_out, not_2_out, and_79_out);
  and and_28 (and_28_out, and_1_out, in_4[12]);
  and and_29 (and_29_out, not_2_out, and_80_out);
  and and_30 (and_30_out, and_1_out, in_4[13]);
  and and_31 (and_31_out, not_2_out, and_81_out);
  and and_32 (and_32_out, and_1_out, in_4[14]);
  and and_33 (and_33_out, not_2_out, and_82_out);
  and and_34 (and_34_out, and_1_out, in_4[15]);
  and and_35 (and_35_out, not_2_out, and_83_out);
  and and_36 (and_36_out, and_1_out, in_4[16]);
  and and_37 (and_37_out, not_2_out, and_84_out);
  and and_38 (and_38_out, and_1_out, in_4[17]);
  and and_39 (and_39_out, not_2_out, and_85_out);
  and and_40 (and_40_out, and_1_out, in_4[18]);
  and and_41 (and_41_out, not_2_out, and_86_out);
  and and_42 (and_42_out, and_1_out, in_4[19]);
  and and_43 (and_43_out, not_2_out, and_87_out);
  and and_44 (and_44_out, and_1_out, in_4[20]);
  and and_45 (and_45_out, not_2_out, and_88_out);
  and and_46 (and_46_out, and_1_out, in_4[21]);
  and and_47 (and_47_out, not_2_out, and_89_out);
  and and_48 (and_48_out, and_1_out, in_4[22]);
  and and_49 (and_49_out, not_2_out, and_90_out);
  and and_50 (and_50_out, and_1_out, in_4[23]);
  and and_51 (and_51_out, not_2_out, and_91_out);
  and and_52 (and_52_out, and_1_out, in_4[24]);
  and and_53 (and_53_out, not_2_out, and_92_out);
  and and_54 (and_54_out, and_1_out, in_4[25]);
  and and_55 (and_55_out, not_2_out, and_93_out);
  and and_56 (and_56_out, and_1_out, in_4[26]);
  and and_57 (and_57_out, not_2_out, and_94_out);
  and and_58 (and_58_out, and_1_out, in_4[27]);
  and and_59 (and_59_out, not_2_out, and_95_out);
  and and_60 (and_60_out, and_1_out, in_4[28]);
  and and_61 (and_61_out, not_2_out, and_96_out);
  and and_62 (and_62_out, and_1_out, in_4[29]);
  and and_63 (and_63_out, not_2_out, and_97_out);
  and and_64 (and_64_out, and_1_out, in_4[30]);
  and and_65 (and_65_out, not_2_out, and_98_out);
  and and_66 (and_66_out, and_1_out, in_4[31]);
  and and_67 (and_67_out, not_2_out, and_99_out);
  or or_1 (or_1_out, and_4_out, and_5_out);
  or or_2 (or_2_out, and_6_out, and_7_out);
  or or_3 (or_3_out, and_8_out, and_9_out);
  or or_4 (or_4_out, and_10_out, and_11_out);
  or or_5 (or_5_out, and_12_out, and_13_out);
  or or_6 (or_6_out, and_14_out, and_15_out);
  or or_7 (or_7_out, and_16_out, and_17_out);
  or or_8 (or_8_out, and_18_out, and_19_out);
  or or_9 (or_9_out, and_20_out, and_21_out);
  or or_10 (or_10_out, and_22_out, and_23_out);
  or or_11 (or_11_out, and_24_out, and_25_out);
  or or_12 (or_12_out, and_26_out, and_27_out);
  or or_13 (or_13_out, and_28_out, and_29_out);
  or or_14 (or_14_out, and_30_out, and_31_out);
  or or_15 (or_15_out, and_32_out, and_33_out);
  or or_16 (or_16_out, and_34_out, and_35_out);
  or or_17 (or_17_out, and_36_out, and_37_out);
  or or_18 (or_18_out, and_38_out, and_39_out);
  or or_19 (or_19_out, and_40_out, and_41_out);
  or or_20 (or_20_out, and_42_out, and_43_out);
  or or_21 (or_21_out, and_44_out, and_45_out);
  or or_22 (or_22_out, and_46_out, and_47_out);
  or or_23 (or_23_out, and_48_out, and_49_out);
  or or_24 (or_24_out, and_50_out, and_51_out);
  or or_25 (or_25_out, and_52_out, and_53_out);
  or or_26 (or_26_out, and_54_out, and_55_out);
  or or_27 (or_27_out, and_56_out, and_57_out);
  or or_28 (or_28_out, and_58_out, and_59_out);
  or or_29 (or_29_out, and_60_out, and_61_out);
  or or_30 (or_30_out, and_62_out, and_63_out);
  or or_31 (or_31_out, and_64_out, and_65_out);
  or or_32 (or_32_out, and_66_out, and_67_out);
  dff dff_1 (.in_1(or_1_out), .out_2(dff_1_out_2));
  and and_68 (and_68_out, out_5[0], not_1_out);
  dff dff_2 (.in_1(or_2_out), .out_2(dff_2_out_2));
  and and_69 (and_69_out, out_5[1], not_1_out);
  dff dff_3 (.in_1(or_3_out), .out_2(dff_3_out_2));
  and and_70 (and_70_out, out_5[2], not_1_out);
  dff dff_4 (.in_1(or_4_out), .out_2(dff_4_out_2));
  and and_71 (and_71_out, out_5[3], not_1_out);
  dff dff_5 (.in_1(or_5_out), .out_2(dff_5_out_2));
  and and_72 (and_72_out, out_5[4], not_1_out);
  dff dff_6 (.in_1(or_6_out), .out_2(dff_6_out_2));
  and and_73 (and_73_out, out_5[5], not_1_out);
  dff dff_7 (.in_1(or_7_out), .out_2(dff_7_out_2));
  and and_74 (and_74_out, out_5[6], not_1_out);
  dff dff_8 (.in_1(or_8_out), .out_2(dff_8_out_2));
  and and_75 (and_75_out, out_5[7], not_1_out);
  dff dff_9 (.in_1(or_9_out), .out_2(dff_9_out_2));
  and and_76 (and_76_out, out_5[8], not_1_out);
  dff dff_10 (.in_1(or_10_out), .out_2(dff_10_out_2));
  and and_77 (and_77_out, out_5[9], not_1_out);
  dff dff_11 (.in_1(or_11_out), .out_2(dff_11_out_2));
  and and_78 (and_78_out, out_5[10], not_1_out);
  dff dff_12 (.in_1(or_12_out), .out_2(dff_12_out_2));
  and and_79 (and_79_out, out_5[11], not_1_out);
  dff dff_13 (.in_1(or_13_out), .out_2(dff_13_out_2));
  and and_80 (and_80_out, out_5[12], not_1_out);
  dff dff_14 (.in_1(or_14_out), .out_2(dff_14_out_2));
  and and_81 (and_81_out, out_5[13], not_1_out);
  dff dff_15 (.in_1(or_15_out), .out_2(dff_15_out_2));
  and and_82 (and_82_out, out_5[14], not_1_out);
  dff dff_16 (.in_1(or_16_out), .out_2(dff_16_out_2));
  and and_83 (and_83_out, out_5[15], not_1_out);
  dff dff_17 (.in_1(or_17_out), .out_2(dff_17_out_2));
  and and_84 (and_84_out, out_5[16], not_1_out);
  dff dff_18 (.in_1(or_18_out), .out_2(dff_18_out_2));
  and and_85 (and_85_out, out_5[17], not_1_out);
  dff dff_19 (.in_1(or_19_out), .out_2(dff_19_out_2));
  and and_86 (and_86_out, out_5[18], not_1_out);
  dff dff_20 (.in_1(or_20_out), .out_2(dff_20_out_2));
  and and_87 (and_87_out, out_5[19], not_1_out);
  dff dff_21 (.in_1(or_21_out), .out_2(dff_21_out_2));
  and and_88 (and_88_out, out_5[20], not_1_out);
  dff dff_22 (.in_1(or_22_out), .out_2(dff_22_out_2));
  and and_89 (and_89_out, out_5[21], not_1_out);
  dff dff_23 (.in_1(or_23_out), .out_2(dff_23_out_2));
  and and_90 (and_90_out, out_5[22], not_1_out);
  dff dff_24 (.in_1(or_24_out), .out_2(dff_24_out_2));
  and and_91 (and_91_out, out_5[23], not_1_out);
  dff dff_25 (.in_1(or_25_out), .out_2(dff_25_out_2));
  and and_92 (and_92_out, out_5[24], not_1_out);
  dff dff_26 (.in_1(or_26_out), .out_2(dff_26_out_2));
  and and_93 (and_93_out, out_5[25], not_1_out);
  dff dff_27 (.in_1(or_27_out), .out_2(dff_27_out_2));
  and and_94 (and_94_out, out_5[26], not_1_out);
  dff dff_28 (.in_1(or_28_out), .out_2(dff_28_out_2));
  and and_95 (and_95_out, out_5[27], not_1_out);
  dff dff_29 (.in_1(or_29_out), .out_2(dff_29_out_2));
  and and_96 (and_96_out, out_5[28], not_1_out);
  dff dff_30 (.in_1(or_30_out), .out_2(dff_30_out_2));
  and and_97 (and_97_out, out_5[29], not_1_out);
  dff dff_31 (.in_1(or_31_out), .out_2(dff_31_out_2));
  and and_98 (and_98_out, out_5[30], not_1_out);
  dff dff_32 (.in_1(or_32_out), .out_2(dff_32_out_2));
  and and_99 (and_99_out, out_5[31], not_1_out);
  xor xor_1 (out_5[0], dff_1_out_2, and_3_out);
  and and_100 (and_100_out, and_3_out, dff_1_out_2);
  xor xor_2 (out_5[1], dff_2_out_2, and_100_out);
  and and_101 (and_101_out, and_100_out, dff_2_out_2);
  xor xor_3 (out_5[2], dff_3_out_2, and_101_out);
  and and_102 (and_102_out, and_101_out, dff_3_out_2);
  xor xor_4 (out_5[3], dff_4_out_2, and_102_out);
  and and_103 (and_103_out, and_102_out, dff_4_out_2);
  xor xor_5 (out_5[4], dff_5_out_2, and_103_out);
  and and_104 (and_104_out, and_103_out, dff_5_out_2);
  xor xor_6 (out_5[5], dff_6_out_2, and_104_out);
  and and_105 (and_105_out, and_104_out, dff_6_out_2);
  xor xor_7 (out_5[6], dff_7_out_2, and_105_out);
  and and_106 (and_106_out, and_105_out, dff_7_out_2);
  xor xor_8 (out_5[7], dff_8_out_2, and_106_out);
  and and_107 (and_107_out, and_106_out, dff_8_out_2);
  xor xor_9 (out_5[8], dff_9_out_2, and_107_out);
  and and_108 (and_108_out, and_107_out, dff_9_out_2);
  xor xor_10 (out_5[9], dff_10_out_2, and_108_out);
  and and_109 (and_109_out, and_108_out, dff_10_out_2);
  xor xor_11 (out_5[10], dff_11_out_2, and_109_out);
  and and_110 (and_110_out, and_109_out, dff_11_out_2);
  xor xor_12 (out_5[11], dff_12_out_2, and_110_out);
  and and_111 (and_111_out, and_110_out, dff_12_out_2);
  xor xor_13 (out_5[12], dff_13_out_2, and_111_out);
  and and_112 (and_112_out, and_111_out, dff_13_out_2);
  xor xor_14 (out_5[13], dff_14_out_2, and_112_out);
  and and_113 (and_113_out, and_112_out, dff_14_out_2);
  xor xor_15 (out_5[14], dff_15_out_2, and_113_out);
  and and_114 (and_114_out, and_113_out, dff_15_out_2);
  xor xor_16 (out_5[15], dff_16_out_2, and_114_out);
  and and_115 (and_115_out, and_114_out, dff_16_out_2);
  xor xor_17 (out_5[16], dff_17_out_2, and_115_out);
  and and_116 (and_116_out, and_115_out, dff_17_out_2);
  xor xor_18 (out_5[17], dff_18_out_2, and_116_out);
  and and_117 (and_117_out, and_116_out, dff_18_out_2);
  xor xor_19 (out_5[18], dff_19_out_2, and_117_out);
  and and_118 (and_118_out, and_117_out, dff_19_out_2);
  xor xor_20 (out_5[19], dff_20_out_2, and_118_out);
  and and_119 (and_119_out, and_118_out, dff_20_out_2);
  xor xor_21 (out_5[20], dff_21_out_2, and_119_out);
  and and_120 (and_120_out, and_119_out, dff_21_out_2);
  xor xor_22 (out_5[21], dff_22_out_2, and_120_out);
  and and_121 (and_121_out, and_120_out, dff_22_out_2);
  xor xor_23 (out_5[22], dff_23_out_2, and_121_out);
  and and_122 (and_122_out, and_121_out, dff_23_out_2);
  xor xor_24 (out_5[23], dff_24_out_2, and_122_out);
  and and_123 (and_123_out, and_122_out, dff_24_out_2);
  xor xor_25 (out_5[24], dff_25_out_2, and_123_out);
  and and_124 (and_124_out, and_123_out, dff_25_out_2);
  xor xor_26 (out_5[25], dff_26_out_2, and_124_out);
  and and_125 (and_125_out, and_124_out, dff_26_out_2);
  xor xor_27 (out_5[26], dff_27_out_2, and_125_out);
  and and_126 (and_126_out, and_125_out, dff_27_out_2);
  xor xor_28 (out_5[27], dff_28_out_2, and_126_out);
  and and_127 (and_127_out, and_126_out, dff_28_out_2);
  xor xor_29 (out_5[28], dff_29_out_2, and_127_out);
  and and_128 (and_128_out, and_127_out, dff_29_out_2);
  xor xor_30 (out_5[29], dff_30_out_2, and_128_out);
  and and_129 (and_129_out, and_128_out, dff_30_out_2);
  xor xor_31 (out_5[30], dff_31_out_2, and_129_out);
  and and_130 (and_130_out, and_129_out, dff_31_out_2);
  xor xor_32 (out_5[31], dff_32_out_2, and_130_out);
endmodule

module dff (
  input  in_1,
  output out_2
);

  wire clock_1_out, nand_1_out, nand_2_out, nand_3_out, nand_4_out, nand_5_out, nand_6_out, nand_7_out,
       not_1_out, not_2_out;

  Clock clock_1 (.out(clock_1_out));
  not not_1 (not_1_out, in_1);
  nand nand_1 (nand_1_out, in_1, clock_1_out);
  nand nand_2 (nand_2_out, nand_1_out, nand_4_out);
  nand nand_3 (nand_3_out, clock_1_out, not_1_out);
  nand nand_4 (nand_4_out, nand_2_out, nand_3_out);
  not not_2 (not_2_out, clock_1_out);
  nand nand_5 (nand_5_out, not_2_out, nand_4_out);
  nand nand_6 (nand_6_out, nand_2_out, not_2_out);
  nand nand_7 (nand_7_out, nand_5_out, out_2);
  nand nand_8 (out_2, nand_7_out, nand_6_out);
endmodule

module mux (
  input  in_1,
  input  in_2,
  input  in_3,
  output out_4
);

  wire nand_1_out, nand_2_out, not_1_out;

  not not_1 (not_1_out, in_1);
  nand nand_1 (nand_1_out, not_1_out, in_2);
  nand nand_2 (nand_2_out, in_1, in_3);
  nand nand_3 (out_4, nand_1_out, nand_2_out);
endmodule

module add (
  input  in_1,
  input  in_2,
  input  in_3,
  output out_4,
  output out_5
);

  wire and_1_out, xor_2_out;

  xor xor_1 (out_4, in_1, xor_2_out);
  xor xor_2 (xor_2_out, in_2, in_3);
  or or_1 (out_5, in_1, and_1_out);
  and and_1 (and_1_out, in_2, in_3);
endmodule

module ALU (
  input  [31:0] a,
  input  [31:0] b,
  input  mode0,
  input  mode1,
  input  sub,
  input  arith,
  input  logic0,
  input  logic1,
  output [31:0] result,
  output zero,
  output neg
);

  wire add_and_or_1_carry, and_1_out, mux_1_out_4, not_33_out, or_1_out, or_2_out, or_3_out, or_4_out,
       or_5_out, or_6_out, or_7_out, or_8_out, or_9_out, or_10_out, or_11_out, or_12_out, or_13_out,
       or_14_out, or_15_out, or_16_out, or_17_out, or_18_out, or_19_out, or_20_out, or_21_out, or_22_out,
       or_23_out, or_24_out, or_25_out, or_26_out, or_27_out, or_28_out, or_29_out, or_30_out, or_31_out,
       or_32_out;
  wire [31:0] add_and_or_1_add_result, add_and_or_1_and_result, add_and_or_1_or_result,
       add_and_or_1_xor_result, mux32_1_out_4, mux32_2_out_4, mux32_3_out_4, mux32_4_out_4, mux32_5_out_4,
       mux32_7_out_4, mux32_8_out_4, not_1_out, shift_1_result;

  and and_1 (and_1_out, mode0, mode1);
  or or_1 (or_1_out, and_1_out, sub);
  not not_1 (not_1_out[0], b[0]);
  not not_2 (not_1_out[1], b[1]);
  not not_3 (not_1_out[2], b[2]);
  not not_4 (not_1_out[3], b[3]);
  not not_5 (not_1_out[4], b[4]);
  not not_6 (not_1_out[5], b[5]);
  not not_7 (not_1_out[6], b[6]);
  not not_8 (not_1_out[7], b[7]);
  not not_9 (not_1_out[8], b[8]);
  not not_10 (not_1_out[9], b[9]);
  not not_11 (not_1_out[10], b[10]);
  not not_12 (not_1_out[11], b[11]);
  not not_13 (not_1_out[12], b[12]);
  not not_14 (not_1_out[13], b[13]);
  not not_15 (not_1_out[14], b[14]);
  not not_16 (not_1_out[15], b[15]);
  not not_17 (not_1_out[16], b[16]);
  not not_18 (not_1_out[17], b[17]);
  not not_19 (not_1_out[18], b[18]);
  not not_20 (not_1_out[19], b[19]);
  not not_21 (not_1_out[20], b[20]);
  not not_22 (not_1_out[21], b[21]);
  not not_23 (not_1_out[22], b[22]);
  not not_24 (not_1_out[23], b[23]);
  not not_25 (not_1_out[24], b[24]);
  not not_26 (not_1_out[25], b[25]);
  not not_27 (not_1_out[26], b[26]);
  not not_28 (not_1_out[27], b[27]);
  not not_29 (not_1_out[28], b[28]);
  not not_30 (not_1_out[29], b[29]);
  not not_31 (not_1_out[30], b[30]);
  not not_32 (not_1_out[31], b[31]);
  mux32 mux32_1 (.in_3(not_1_out), .in_2(b), .in_1(or_1_out), .out_4(mux32_1_out_4));
  shift shift_1 (.right(sub), .arith(arith), .b(b[4:0]), .a(a), .result(shift_1_result));
  add_and_or add_and_or_1 (
    .b(mux32_1_out_4), .a(a), .neg(or_1_out), .xor_result(add_and_or_1_xor_result),
    .add_result(add_and_or_1_add_result), .and_result(add_and_or_1_and_result),
    .or_result(add_and_or_1_or_result), .carry(add_and_or_1_carry));
  not not_33 (not_33_out, add_and_or_1_carry);
  mux mux_1 (.in_2(add_and_or_1_add_result[31]), .in_3(not_33_out), .in_1(arith), .out_4(mux_1_out_4));
  mux32 mux32_2 (.in_3(mux32_7_out_4), .in_2(add_and_or_1_add_result), .in_1(mode0), .out_4(mux32_2_out_4));
  mux32 mux32_3 (.in_3(add_and_or_1_or_result), .in_2(add_and_or_1_and_result), .in_1(logic0), .out_4(mux32_3_out_4));
  mux32 mux32_4 (.in_3(b), .in_2(add_and_or_1_xor_result), .in_1(logic0), .out_4(mux32_4_out_4));
  mux32 mux32_5 (.in_3(32'h1), .in_2({32{1'b0}}), .in_1(mux_1_out_4), .out_4(mux32_5_out_4));
  mux32 mux32_6 (.in_3(mux32_8_out_4), .in_2(mux32_2_out_4), .in_1(mode1), .out_4({neg, result[30:0]}));
  mux32 mux32_7 (.in_3(mux32_4_out_4), .in_2(mux32_3_out_4), .in_1(logic1), .out_4(mux32_7_out_4));
  mux32 mux32_8 (.in_3(mux32_5_out_4), .in_2(shift_1_result), .in_1(mode0), .out_4(mux32_8_out_4));
  or or_2 (or_2_out, result[0], result[1]);
  or or_3 (or_3_out, result[2], result[3]);
  or or_4 (or_4_out, result[4], result[5]);
  or or_5 (or_5_out, result[6], result[7]);
  or or_6 (or_6_out, result[8], result[9]);
  or or_7 (or_7_out, result[10], result[11]);
  or or_8 (or_8_out, result[12], result[13]);
  or or_9 (or_9_out, result[14], result[15]);
  or or_10 (or_10_out, result[16], result[17]);
  or or_11 (or_11_out, result[18], result[19]);
  or or_12 (or_12_out, result[20], result[21]);
  or or_13 (or_13_out, result[22], result[23]);
  or or_14 (or_14_out, result[24], result[25]);
  or or_15 (or_15_out, result[26], result[27]);
  or or_16 (or_16_out, result[28], result[29]);
  or or_17 (or_17_out, result[30], neg);
  or or_18 (or_18_out, or_2_out, or_3_out);
  or or_19 (or_19_out, or_18_out, or_20_out);
  or or_20 (or_20_out, or_4_out, or_5_out);
  or or_21 (or_21_out, or_19_out, or_23_out);
  or or_22 (or_22_out, or_6_out, or_7_out);
  or or_23 (or_23_out, or_22_out, or_24_out);
  or or_24 (or_24_out, or_8_out, or_9_out);
  or or_25 (or_25_out, or_21_out, or_29_out);
  not not_34 (zero, or_25_out);
  or or_26 (or_26_out, or_10_out, or_11_out);
  or or_27 (or_27_out, or_26_out, or_28_out);
  or or_28 (or_28_out, or_12_out, or_13_out);
  or or_29 (or_29_out, or_27_out, or_31_out);
  or or_30 (or_30_out, or_14_out, or_15_out);
  or or_31 (or_31_out, or_30_out, or_32_out);
  or or_32 (or_32_out, or_16_out, or_17_out);

  assign result[31] = neg;
endmodule

module select_register (
  input  [4:0] rs1,
  input  load1,
  input  [4:0] rs2,
  input  load2,
  input  [4:0] rd,
  input  store,
  input  [31:0] in1,
  output [31:0] out1,
  output [31:0] out2
);

  wire dmux32way_1_out_3, dmux32way_1_out_4, dmux32way_1_out_5, dmux32way_1_out_6, dmux32way_1_out_7,
       dmux32way_1_out_8, dmux32way_1_out_9, dmux32way_1_out_10, dmux32way_1_out_11, dmux32way_1_out_12,
       dmux32way_1_out_13, dmux32way_1_out_14, dmux32way_1_out_15, dmux32way_1_out_16, dmux32way_1_out_17,
       dmux32way_1_out_18, dmux32way_1_out_19, dmux32way_1_out_20, dmux32way_1_out_21, dmux32way_1_out_22,
       dmux32way_1_out_23, dmux32way_1_out_24, dmux32way_1_out_25, dmux32way_1_out_26, dmux32way_1_out_27,
       dmux32way_1_out_28, dmux32way_1_out_29, dmux32way_1_out_30, dmux32way_1_out_31, dmux32way_1_out_32,
       dmux32way_1_out_33, dmux32way_1_out_34;
  wire [31:0] bit32_1_out_3, mux32bit32way_1_out_34, mux32bit32way_2_out_34, undriven, undriven_2,
       undriven_3, undriven_4, undriven_5, undriven_6, undriven_7, undriven_8, undriven_9, undriven_10,
       undriven_11, undriven_12, undriven_13, undriven_14, undriven_15, undriven_16, undriven_17,
       undriven_18, undriven_19, undriven_20, undriven_21, undriven_22, undriven_23, undriven_24,
       undriven_25, undriven_26, undriven_27, undriven_28, undriven_29, undriven_30, undriven_31;

  dmux32way dmux32way_1 (
    .in_1(rd), .in_2(store), .out_25(dmux32way_1_out_25), .out_26(dmux32way_1_out_26),
    .out_27(dmux32way_1_out_27), .out_28(dmux32way_1_out_28), .out_29(dmux32way_1_out_29),
    .out_30(dmux32way_1_out_30), .out_31(dmux32way_1_out_31), .out_32(dmux32way_1_out_32),
    .out_3(dmux32way_1_out_3), .out_33(dmux32way_1_out_33), .out_34(dmux32way_1_out_34),
    .out_4(dmux32way_1_out_4), .out_5(dmux32way_1_out_5), .out_6(dmux32way_1_out_6),
    .out_7(dmux32way_1_out_7), .out_8(dmux32way_1_out_8), .out_9(dmux32way_1_out_9),
    .out_10(dmux32way_1_out_10), .out_11(dmux32way_1_out_11), .out_12(dmux32way_1_out_12),
    .out_13(dmux32way_1_out_13), .out_14(dmux32way_1_out_14), .out_15(dmux32way_1_out_15),
    .out_16(dmux32way_1_out_16), .out_17(dmux32way_1_out_17), .out_18(dmux32way_1_out_18),
    .out_19(dmux32way_1_out_19), .out_20(dmux32way_1_out_20), .out_21(dmux32way_1_out_21),
    .out_22(dmux32way_1_out_22), .out_23(dmux32way_1_out_23), .out_24(dmux32way_1_out_24));
  bit32 bit32_1 (.load(dmux32way_1_out_3), .in_2(in1), .out_3(bit32_1_out_3));
  mux32bit32way mux32bit32way_1 (
    .in_1(rs1), .in_31(undriven_29), .in_32(undriven_30), .in_33(undriven_31), .in_2(bit32_1_out_3),
    .in_3(undriven), .in_4(undriven_2), .in_5(undriven_3), .in_6(undriven_4), .in_7(undriven_5),
    .in_8(undriven_6), .in_9(undriven_7), .in_10(undriven_8), .in_11(undriven_9), .in_12(undriven_10),
    .in_13(undriven_11), .in_14(undriven_12), .in_15(undriven_13), .in_16(undriven_14), .in_17(undriven_15),
    .in_18(undriven_16), .in_19(undriven_17), .in_20(undriven_18), .in_21(undriven_19), .in_22(undriven_20),
    .in_23(undriven_21), .in_24(undriven_22), .in_25(undriven_23), .in_26(undriven_24), .in_27(undriven_25),
    .in_28(undriven_26), .in_29(undriven_27), .in_30(undriven_28), .out_34(mux32bit32way_1_out_34));
  mux32bit32way mux32bit32way_2 (
    .in_1(rs2), .in_31(undriven_29), .in_32(undriven_30), .in_33(undriven_31), .in_2(bit32_1_out_3),
    .in_3(undriven), .in_4(undriven_2), .in_5(undriven_3), .in_6(undriven_4), .in_7(undriven_5),
    .in_8(undriven_6), .in_9(undriven_7), .in_10(undriven_8), .in_11(undriven_9), .in_12(undriven_10),
    .in_13(undriven_11), .in_14(undriven_12), .in_15(undriven_13), .in_16(undriven_14), .in_17(undriven_15),
    .in_18(undriven_16), .in_19(undriven_17), .in_20(undriven_18), .in_21(undriven_19), .in_22(undriven_20),
    .in_23(undriven_21), .in_24(undriven_22), .in_25(undriven_23), .in_26(undriven_24), .in_27(undriven_25),
    .in_28(undriven_26), .in_29(undriven_27), .in_30(undriven_28), .out_34(mux32bit32way_2_out_34));
  mux32 mux32_1 (.in_3(mux32bit32way_1_out_34), .in_2({32{1'b0}}), .in_1(load1), .out_4(out1));
  mux32 mux32_2 (.in_3(mux32bit32way_2_out_34), .in_2({32{1'b0}}), .in_1(load2), .out_4(out2));
endmodule

module \bit  (
  input  load,
  input  in_2,
  output out_3
);

  wire clock_1_out, nand_1_out, nand_2_out, nand_3_out, nand_4_out, nand_5_out, nand_6_out, nand_7_out,
       nand_8_out, nand_9_out, nand_10_out, nand_11_out, nand_12_out, nand_13_out;

  Clock clock_1 (.out(clock_1_out));
  nand nand_1 (nand_1_out, load, load);
  nand nand_2 (nand_2_out, nand_1_out, out_3);
  nand nand_3 (nand_3_out, load, in_2);
  nand nand_4 (nand_4_out, nand_2_out, nand_3_out);
  nand nand_5 (nand_5_out, nand_4_out, nand_4_out);
  nand nand_6 (nand_6_out, nand_4_out, clock_1_out);
  nand nand_7 (nand_7_out, nand_6_out, nand_10_out);
  nand nand_8 (nand_8_out, clock_1_out, nand_5_out);
  nand nand_9 (nand_9_out, nand_7_out, nand_11_out);
  nand nand_10 (nand_10_out, nand_7_out, nand_8_out);
  nand nand_11 (nand_11_out, clock_1_out, clock_1_out);
  nand nand_12 (nand_12_out, nand_11_out, nand_10_out);
  nand nand_13 (nand_13_out, nand_12_out, out_3);
  nand nand_14 (out_3, nand_13_out, nand_9_out);
endmodule

module mux32 (
  input  in_1,
  input  [31:0] in_2,
  input  [31:0] in_3,
  output [31:0] out_4
);

  wire nand_1_out, nand_2_out, nand_3_out, nand_4_out, nand_5_out, nand_6_out, nand_7_out, nand_8_out,
       nand_9_out, nand_10_out, nand_11_out, nand_12_out, nand_13_out, nand_14_out, nand_15_out, nand_16_out,
       nand_17_out, nand_18_out, nand_19_out, nand_20_out, nand_21_out, nand_22_out, nand_23_out,
       nand_24_out, nand_25_out, nand_26_out, nand_27_out, nand_28_out, nand_29_out, nand_30_out,
       nand_31_out, nand_32_out, nand_33_out, nand_34_out, nand_35_out, nand_36_out, nand_37_out,
       nand_38_out, nand_39_out, nand_40_out, nand_41_out, nand_42_out, nand_43_out, nand_44_out,
       nand_45_out, nand_46_out, nand_47_out, nand_48_out, nand_49_out, nand_50_out, nand_51_out,
       nand_52_out, nand_53_out, nand_54_out, nand_55_out, nand_56_out, nand_57_out, nand_58_out,
       nand_59_out, nand_60_out, nand_61_out, nand_62_out, nand_63_out, nand_64_out, not_1_out;

  not not_1 (not_1_out, in_1);
  nand nand_1 (nand_1_out, not_1_out, in_2[0]);
  nand nand_2 (nand_2_out, in_1, in_3[0]);
  nand nand_3 (nand_3_out, not_1_out, in_2[1]);
  nand nand_4 (nand_4_out, in_1, in_3[1]);
  nand nand_5 (nand_5_out, not_1_out, in_2[2]);
  nand nand_6 (nand_6_out, in_1, in_3[2]);
  nand nand_7 (nand_7_out, not_1_out, in_2[3]);
  nand nand_8 (nand_8_out, in_1, in_3[3]);
  nand nand_9 (nand_9_out, not_1_out, in_2[4]);
  nand nand_10 (nand_10_out, in_1, in_3[4]);
  nand nand_11 (nand_11_out, not_1_out, in_2[5]);
  nand nand_12 (nand_12_out, in_1, in_3[5]);
  nand nand_13 (nand_13_out, not_1_out, in_2[6]);
  nand nand_14 (nand_14_out, in_1, in_3[6]);
  nand nand_15 (nand_15_out, not_1_out, in_2[7]);
  nand nand_16 (nand_16_out, in_1, in_3[7]);
  nand nand_17 (nand_17_out, not_1_out, in_2[8]);
  nand nand_18 (nand_18_out, in_1, in_3[8]);
  nand nand_19 (nand_19_out, not_1_out, in_2[9]);
  nand nand_20 (nand_20_out, in_1, in_3[9]);
  nand nand_21 (nand_21_out, not_1_out, in_2[10]);
  nand nand_22 (nand_22_out, in_1, in_3[10]);
  nand nand_23 (nand_23_out, not_1_out, in_2[11]);
  nand nand_24 (nand_24_out, in_1, in_3[11]);
  nand nand_25 (nand_25_out, not_1_out, in_2[12]);
  nand nand_26 (nand_26_out, in_1, in_3[12]);
  nand nand_27 (nand_27_out, not_1_out, in_2[13]);
  nand nand_28 (nand_28_out, in_1, in_3[13]);
  nand nand_29 (nand_29_out, not_1_out, in_2[14]);
  nand nand_30 (nand_30_out, in_1, in_3[14]);
  nand nand_31 (nand_31_out, not_1_out, in_2[15]);
  nand nand_32 (nand_32_out, in_1, in_3[15]);
  nand nand_33 (nand_33_out, not_1_out, in_2[16]);
  nand nand_34 (nand_34_out, in_1, in_3[16]);
  nand nand_35 (nand_35_out, not_1_out, in_2[17]);
  nand nand_36 (nand_36_out, in_1, in_3[17]);
  nand nand_37 (nand_37_out, not_1_out, in_2[18]);
  nand nand_38 (nand_38_out, in_1, in_3[18]);
  nand nand_39 (nand_39_out, not_1_out, in_2[19]);
  nand nand_40 (nand_40_out, in_1, in_3[19]);
  nand nand_41 (nand_41_out, not_1_out, in_2[20]);
  nand nand_42 (nand_42_out, in_1, in_3[20]);
  nand nand_43 (nand_43_out, not_1_out, in_2[21]);
  nand nand_44 (nand_44_out, in_1, in_3[21]);
  nand nand_45 (nand_45_out, not_1_out, in_2[22]);
  nand nand_46 (nand_46_out, in_1, in_3[22]);
  nand nand_47 (nand_47_out, not_1_out, in_2[23]);
  nand nand_48 (nand_48_out, in_1, in_3[23]);
  nand nand_49 (nand_49_out, not_1_out, in_2[24]);
  nand nand_50 (nand_50_out, in_1, in_3[24]);
  nand nand_51 (nand_51_out, not_1_out, in_2[25]);
  nand nand_52 (nand_52_out, in_1, in_3[25]);
  nand nand_53 (nand_53_out, not_1_out, in_2[26]);
  nand nand_54 (nand_54_out, in_1, in_3[26]);
  nand nand_55 (nand_55_out, not_1_out, in_2[27]);
  nand nand_56 (nand_56_out, in_1, in_3[27]);
  nand nand_57 (nand_57_out, not_1_out, in_2[28]);
  nand nand_58 (nand_58_out, in_1, in_3[28]);
  nand nand_59 (nand_59_out, not_1_out, in_2[29]);
  nand nand_60 (nand_60_out, in_1, in_3[29]);
  nand nand_61 (nand_61_out, not_1_out, in_2[30]);
  nand nand_62 (nand_62_out, in_1, in_3[30]);
  nand nand_63 (nand_63_out, not_1_out, in_2[31]);
  nand nand_64 (nand_64_out, in_1, in_3[31]);
  nand nand_65 (out_4[0], nand_1_out, nand_2_out);
  nand nand_66 (out_4[1], nand_3_out, nand_4_out);
  nand nand_67 (out_4[2], nand_5_out, nand_6_out);
  nand nand_68 (out_4[3], nand_7_out, nand_8_out);
  nand nand_69 (out_4[4], nand_9_out, nand_10_out);
  nand nand_70 (out_4[5], nand_11_out, nand_12_out);
  nand nand_71 (out_4[6], nand_13_out, nand_14_out);
  nand nand_72 (out_4[7], nand_15_out, nand_16_out);
  nand nand_73 (out_4[8], nand_17_out, nand_18_out);
  nand nand_74 (out_4[9], nand_19_out, nand_20_out);
  nand nand_75 (out_4[10], nand_21_out, nand_22_out);
  nand nand_76 (out_4[11], nand_23_out, nand_24_out);
  nand nand_77 (out_4[12], nand_25_out, nand_26_out);
  nand nand_78 (out_4[13], nand_27_out, nand_28_out);
  nand nand_79 (out_4[14], nand_29_out, nand_30_out);
  nand nand_80 (out_4[15], nand_31_out, nand_32_out);
  nand nand_81 (out_4[16], nand_33_out, nand_34_out);
  nand nand_82 (out_4[17], nand_35_out, nand_36_out);
  nand nand_83 (out_4[18], nand_37_out, nand_38_out);
  nand nand_84 (out_4[19], nand_39_out, nand_40_out);
  nand nand_85 (out_4[20], nand_41_out, nand_42_out);
  nand nand_86 (out_4[21], nand_43_out, nand_44_out);
  nand nand_87 (out_4[22], nand_45_out, nand_46_out);
  nand nand_88 (out_4[23], nand_47_out, nand_48_out);
  nand nand_89 (out_4[24], nand_49_out, nand_50_out);
  nand nand_90 (out_4[25], nand_51_out, nand_52_out);
  nand nand_91 (out_4[26], nand_53_out, nand_54_out);
  nand nand_92 (out_4[27], nand_55_out, nand_56_out);
  nand nand_93 (out_4[28], nand_57_out, nand_58_out);
  nand nand_94 (out_4[29], nand_59_out, nand_60_out);
  nand nand_95 (out_4[30], nand_61_out, nand_62_out);
  nand nand_96 (out_4[31], nand_63_out, nand_64_out);
endmodule

module sign (
  input  [31:0] value,
  input  [3:0] read,
  input  unsign,
  output [31:0] result
);

  wire and_1_out, and_2_out, and_3_out, and_4_out, and_5_out, and_6_out, and_7_out, not_1_out, not_2_out,
       not_3_out, not_4_out, or_1_out, or_2_out, or_3_out;
  wire [7:0] mux8_1_out_4, mux8_2_out_4, mux8_3_out_4, mux8_4_out_4, mux8_5_out_4, mux8_6_out_4,
       mux8_7_out_4, mux8_12_out_4, mux8_13_out_4, mux8_14_out_4;

  and and_1 (and_1_out, read[3], read[2]);
  and and_2 (and_2_out, read[1], read[0]);
  not not_1 (not_1_out, read[0]);
  and and_3 (and_3_out, not_1_out, not_2_out);
  not not_2 (not_2_out, read[1]);
  not not_3 (not_3_out, read[2]);
  and and_4 (and_4_out, not_3_out, not_4_out);
  not not_4 (not_4_out, read[3]);
  and and_5 (and_5_out, and_1_out, and_2_out);
  or or_1 (or_1_out, read[2], read[3]);
  or or_2 (or_2_out, read[1], read[3]);
  and and_6 (and_6_out, and_1_out, and_3_out);
  or or_3 (or_3_out, and_6_out, and_7_out);
  and and_7 (and_7_out, and_4_out, and_2_out);
  mux8 mux8_1 (.in_1(or_2_out), .in_3(value[15:8]), .in_2(value[7:0]), .out_4(mux8_1_out_4));
  mux8 mux8_2 (.in_1(or_2_out), .in_3(value[31:24]), .in_2(value[23:16]), .out_4(mux8_2_out_4));
  mux8 mux8_3 (.in_1(or_1_out), .in_3(mux8_2_out_4), .in_2(mux8_1_out_4), .out_4(mux8_3_out_4));
  mux8 mux8_4 (.in_1(and_6_out), .in_3(value[23:16]), .in_2(value[7:0]), .out_4(mux8_4_out_4));
  mux8 mux8_5 (.in_1(and_6_out), .in_3(value[31:24]), .in_2(value[15:8]), .out_4(mux8_5_out_4));
  mux8 mux8_6 (.in_1(or_3_out), .in_3(mux8_4_out_4), .in_2(mux8_3_out_4), .out_4(mux8_6_out_4));
  mux8 mux8_7 (.in_1(or_3_out), .in_3(mux8_5_out_4), .in_2(mux8_12_out_4), .out_4(mux8_7_out_4));
  mux8 mux8_8 (.in_1(and_5_out), .in_3(value[7:0]), .in_2(mux8_6_out_4), .out_4(result[7:0]));
  mux8 mux8_9 (.in_1(and_5_out), .in_3(value[15:8]), .in_2(mux8_7_out_4), .out_4(result[15:8]));
  mux8 mux8_10 (.in_1(and_5_out), .in_3(value[23:16]), .in_2(mux8_14_out_4), .out_4(result[23:16]));
  mux8 mux8_11 (.in_1(and_5_out), .in_3(value[31:24]), .in_2(mux8_14_out_4), .out_4(result[31:24]));
  mux8 mux8_12 (.in_1(unsign), .in_3({8{1'b0}}), .in_2({8{mux8_3_out_4[7]}}), .out_4(mux8_12_out_4));
  mux8 mux8_13 (.in_1(unsign), .in_3({8{1'b0}}), .in_2({8{mux8_5_out_4[7]}}), .out_4(mux8_13_out_4));
  mux8 mux8_14 (.in_1(or_3_out), .in_3(mux8_13_out_4), .in_2(mux8_12_out_4), .out_4(mux8_14_out_4));
endmodule

module mux8 (
  input  in_1,
  input  [7:0] in_2,
  input  [7:0] in_3,
  output [7:0] out_4
);

  wire nand_1_out, nand_3_out, nand_4_out, nand_6_out, nand_7_out, nand_9_out, nand_10_out, nand_12_out,
       nand_13_out, nand_15_out, nand_16_out, nand_18_out, nand_19_out, nand_21_out, nand_22_out,
       nand_24_out, not_1_out;

  not not_1 (not_1_out, in_1);
  nand nand_1 (nand_1_out, not_1_out, in_2[0]);
  nand nand_2 (out_4[0], nand_1_out, nand_3_out);
  nand nand_3 (nand_3_out, in_1, in_3[0]);
  nand nand_4 (nand_4_out, not_1_out, in_2[1]);
  nand nand_5 (out_4[1], nand_4_out, nand_6_out);
  nand nand_6 (nand_6_out, in_1, in_3[1]);
  nand nand_7 (nand_7_out, not_1_out, in_2[2]);
  nand nand_8 (out_4[2], nand_7_out, nand_9_out);
  nand nand_9 (nand_9_out, in_1, in_3[2]);
  nand nand_10 (nand_10_out, not_1_out, in_2[3]);
  nand nand_11 (out_4[3], nand_10_out, nand_12_out);
  nand nand_12 (nand_12_out, in_1, in_3[3]);
  nand nand_13 (nand_13_out, not_1_out, in_2[4]);
  nand nand_14 (out_4[4], nand_13_out, nand_15_out);
  nand nand_15 (nand_15_out, in_1, in_3[4]);
  nand nand_16 (nand_16_out, not_1_out, in_2[5]);
  nand nand_17 (out_4[5], nand_16_out, nand_18_out);
  nand nand_18 (nand_18_out, in_1, in_3[5]);
  nand nand_19 (nand_19_out, not_1_out, in_2[6]);
  nand nand_20 (out_4[6], nand_19_out, nand_21_out);
  nand nand_21 (nand_21_out, in_1, in_3[6]);
  nand nand_22 (nand_22_out, not_1_out, in_2[7]);
  nand nand_23 (out_4[7], nand_22_out, nand_24_out);
  nand nand_24 (nand_24_out, in_1, in_3[7]);
endmodule

module add_and_or (
  input  neg,
  input  [31:0] a,
  input  [31:0] b,
  output [31:0] or_result,
  output [31:0] xor_result,
  output [31:0] add_result,
  output [31:0] and_result,
  output carry
);

  wire and_33_out, and_34_out, and_35_out, and_36_out, and_37_out, and_38_out, and_39_out, and_40_out,
       and_41_out, and_42_out, and_43_out, and_44_out, and_45_out, and_46_out, and_47_out, and_48_out,
       and_49_out, and_50_out, and_51_out, and_52_out, and_53_out, and_54_out, and_55_out, and_56_out,
       and_57_out, and_58_out, and_59_out, and_60_out, and_61_out, and_62_out, and_63_out, and_64_out,
       or_33_out, or_34_out, or_35_out, or_36_out, or_37_out, or_38_out, or_39_out, or_40_out, or_41_out,
       or_42_out, or_43_out, or_44_out, or_45_out, or_46_out, or_47_out, or_48_out, or_49_out, or_50_out,
       or_51_out, or_52_out, or_53_out, or_54_out, or_55_out, or_56_out, or_57_out, or_58_out, or_59_out,
       or_60_out, or_61_out, or_62_out, or_63_out;

  or or_1 (or_result[0], a[0], b[0]);
  xor xor_1 (xor_result[0], a[0], b[0]);
  and and_1 (and_result[0], b[0], a[0]);
  or or_2 (or_result[1], a[1], b[1]);
  xor xor_2 (xor_result[1], a[1], b[1]);
  and and_2 (and_result[1], b[1], a[1]);
  or or_3 (or_result[2], a[2], b[2]);
  xor xor_3 (xor_result[2], a[2], b[2]);
  and and_3 (and_result[2], b[2], a[2]);
  or or_4 (or_result[3], a[3], b[3]);
  xor xor_4 (xor_result[3], a[3], b[3]);
  and and_4 (and_result[3], b[3], a[3]);
  or or_5 (or_result[4], a[4], b[4]);
  xor xor_5 (xor_result[4], a[4], b[4]);
  and and_5 (and_result[4], b[4], a[4]);
  or or_6 (or_result[5], a[5], b[5]);
  xor xor_6 (xor_result[5], a[5], b[5]);
  and and_6 (and_result[5], b[5], a[5]);
  or or_7 (or_result[6], a[6], b[6]);
  xor xor_7 (xor_result[6], a[6], b[6]);
  and and_7 (and_result[6], b[6], a[6]);
  or or_8 (or_result[7], a[7], b[7]);
  xor xor_8 (xor_result[7], a[7], b[7]);
  and and_8 (and_result[7], b[7], a[7]);
  or or_9 (or_result[8], a[8], b[8]);
  xor xor_9 (xor_result[8], a[8], b[8]);
  and and_9 (and_result[8], b[8], a[8]);
  or or_10 (or_result[9], a[9], b[9]);
  xor xor_10 (xor_result[9], a[9], b[9]);
  and and_10 (and_result[9], b[9], a[9]);
  or or_11 (or_result[10], a[10], b[10]);
  xor xor_11 (xor_result[10], a[10], b[10]);
  and and_11 (and_result[10], b[10], a[10]);
  or or_12 (or_result[11], a[11], b[11]);
  xor xor_12 (xor_result[11], a[11], b[11]);
  and and_12 (and_result[11], b[11], a[11]);
  or or_13 (or_result[12], a[12], b[12]);
  xor xor_13 (xor_result[12], a[12], b[12]);
  and and_13 (and_result[12], b[12], a[12]);
  or or_14 (or_result[13], a[13], b[13]);
  xor xor_14 (xor_result[13], a[13], b[13]);
  and and_14 (and_result[13], b[13], a[13]);
  or or_15 (or_result[14], a[14], b[14]);
  xor xor_15 (xor_result[14], a[14], b[14]);
  and and_15 (and_result[14], b[14], a[14]);
  or or_16 (or_result[15], a[15], b[15]);
  xor xor_16 (xor_result[15], a[15], b[15]);
  and and_16 (and_result[15], b[15], a[15]);
  or or_17 (or_result[16], a[16], b[16]);
  xor xor_17 (xor_result[16], a[16], b[16]);
  and and_17 (and_result[16], b[16], a[16]);
  or or_18 (or_result[17], a[17], b[17]);
  xor xor_18 (xor_result[17], a[17], b[17]);
  and and_18 (and_result[17], b[17], a[17]);
  or or_19 (or_result[18], a[18], b[18]);
  xor xor_19 (xor_result[18], a[18], b[18]);
  and and_19 (and_result[18], b[18], a[18]);
  or or_20 (or_result[19], a[19], b[19]);
  xor xor_20 (xor_result[19], a[19], b[19]);
  and and_20 (and_result[19], b[19], a[19]);
  or or_21 (or_result[20], a[20], b[20]);
  xor xor_21 (xor_result[20], a[20], b[20]);
  and and_21 (and_result[20], b[20], a[20]);
  or or_22 (or_result[21], a[21], b[21]);
  xor xor_22 (xor_result[21], a[21], b[21]);
  and and_22 (and_result[21], b[21], a[21]);
  or or_23 (or_result[22], a[22], b[22]);
  xor xor_23 (xor_result[22], a[22], b[22]);
  and and_23 (and_result[22], b[22], a[22]);
  or or_24 (or_result[23], a[23], b[23]);
  xor xor_24 (xor_result[23], a[23], b[23]);
  and and_24 (and_result[23], b[23], a[23]);
  or or_25 (or_result[24], a[24], b[24]);
  xor xor_25 (xor_result[24], a[24], b[24]);
  and and_25 (and_result[24], b[24], a[24]);
  or or_26 (or_result[25], a[25], b[25]);
  xor xor_26 (xor_result[25], a[25], b[25]);
  and and_26 (and_result[25], b[25], a[25]);
  or or_27 (or_result[26], a[26], b[26]);
  xor xor_27 (xor_result[26], a[26], b[26]);
  and and_27 (and_result[26], b[26], a[26]);
  or or_28 (or_result[27], a[27], b[27]);
  xor xor_28 (xor_result[27], a[27], b[27]);
  and and_28 (and_result[27], b[27], a[27]);
  or or_29 (or_result[28], a[28], b[28]);
  xor xor_29 (xor_result[28], a[28], b[28]);
  and and_29 (and_result[28], b[28], a[28]);
  or or_30 (or_result[29], a[29], b[29]);
  xor xor_30 (xor_result[29], a[29], b[29]);
  and and_30 (and_result[29], b[29], a[29]);
  or or_31 (or_result[30], a[30], b[30]);
  xor xor_31 (xor_result[30], a[30], b[30]);
  and and_31 (and_result[30], b[30], a[30]);
  or or_32 (or_result[31], a[31], b[31]);
  xor xor_32 (xor_result[31], a[31], b[31]);
  and and_32 (and_result[31], b[31], a[31]);
  xor xor_33 (add_result[0], neg, xor_result[0]);
  and and_33 (and_33_out, neg, xor_result[0]);
  or or_33 (or_33_out, and_33_out, and_result[0]);
  xor xor_34 (add_result[1], or_33_out, xor_result[1]);
  and and_34 (and_34_out, or_33_out, xor_result[1]);
  or or_34 (or_34_out, and_34_out, and_result[1]);
  xor xor_35 (add_result[2], or_34_out, xor_result[2]);
  and and_35 (and_35_out, or_34_out, xor_result[2]);
  or or_35 (or_35_out, and_35_out, and_result[2]);
  xor xor_36 (add_result[3], or_35_out, xor_result[3]);
  and and_36 (and_36_out, or_35_out, xor_result[3]);
  or or_36 (or_36_out, and_36_out, and_result[3]);
  xor xor_37 (add_result[4], or_36_out, xor_result[4]);
  and and_37 (and_37_out, or_36_out, xor_result[4]);
  or or_37 (or_37_out, and_37_out, and_result[4]);
  xor xor_38 (add_result[5], or_37_out, xor_result[5]);
  and and_38 (and_38_out, or_37_out, xor_result[5]);
  or or_38 (or_38_out, and_38_out, and_result[5]);
  xor xor_39 (add_result[6], or_38_out, xor_result[6]);
  and and_39 (and_39_out, or_38_out, xor_result[6]);
  or or_39 (or_39_out, and_39_out, and_result[6]);
  xor xor_40 (add_result[7], or_39_out, xor_result[7]);
  and and_40 (and_40_out, or_39_out, xor_result[7]);
  or or_40 (or_40_out, and_40_out, and_result[7]);
  xor xor_41 (add_result[8], or_40_out, xor_result[8]);
  and and_41 (and_41_out, or_40_out, xor_result[8]);
  or or_41 (or_41_out, and_41_out, and_result[8]);
  xor xor_42 (add_result[9], or_41_out, xor_result[9]);
  and and_42 (and_42_out, or_41_out, xor_result[9]);
  or or_42 (or_42_out, and_42_out, and_result[9]);
  xor xor_43 (add_result[10], or_42_out, xor_result[10]);
  and and_43 (and_43_out, or_42_out, xor_result[10]);
  or or_43 (or_43_out, and_43_out, and_result[10]);
  xor xor_44 (add_result[11], or_43_out, xor_result[11]);
  and and_44 (and_44_out, or_43_out, xor_result[11]);
  or or_44 (or_44_out, and_44_out, and_result[11]);
  xor xor_45 (add_result[12], or_44_out, xor_result[12]);
  and and_45 (and_45_out, or_44_out, xor_result[12]);
  or or_45 (or_45_out, and_45_out, and_result[12]);
  xor xor_46 (add_result[13], or_45_out, xor_result[13]);
  and and_46 (and_46_out, or_45_out, xor_result[13]);
  or or_46 (or_46_out, and_46_out, and_result[13]);
  xor xor_47 (add_result[14], or_46_out, xor_result[14]);
  and and_47 (and_47_out, or_46_out, xor_result[14]);
  or or_47 (or_47_out, and_47_out, and_result[14]);
  xor xor_48 (add_result[15], or_47_out, xor_result[15]);
  and and_48 (and_48_out, or_47_out, xor_result[15]);
  or or_48 (or_48_out, and_48_out, and_result[15]);
  xor xor_49 (add_result[16], or_48_out, xor_result[16]);
  and and_49 (and_49_out, or_48_out, xor_result[16]);
  or or_49 (or_49_out, and_49_out, and_result[16]);
  xor xor_50 (add_result[17], or_49_out, xor_result[17]);
  and and_50 (and_50_out, or_49_out, xor_result[17]);
  or or_50 (or_50_out, and_50_out, and_result[17]);
  xor xor_51 (add_result[18], or_50_out, xor_result[18]);
  and and_51 (and_51_out, or_50_out, xor_result[18]);
  or or_51 (or_51_out, and_51_out, and_result[18]);
  xor xor_52 (add_result[19], or_51_out, xor_result[19]);
  and and_52 (and_52_out, or_51_out, xor_result[19]);
  or or_52 (or_52_out, and_52_out, and_result[19]);
  xor xor_53 (add_result[20], or_52_out, xor_result[20]);
  and and_53 (and_53_out, or_52_out, xor_result[20]);
  or or_53 (or_53_out, and_53_out, and_result[20]);
  xor xor_54 (add_result[21], or_53_out, xor_result[21]);
  and and_54 (and_54_out, or_53_out, xor_result[21]);
  or or_54 (or_54_out, and_54_out, and_result[21]);
  xor xor_55 (add_result[22], or_54_out, xor_result[22]);
  and and_55 (and_55_out, or_54_out, xor_result[22]);
  or or_55 (or_55_out, and_55_out, and_result[22]);
  xor xor_56 (add_result[23], or_55_out, xor_result[23]);
  and and_56 (and_56_out, or_55_out, xor_result[23]);
  or or_56 (or_56_out, and_56_out, and_result[23]);
  xor xor_57 (add_result[24], or_56_out, xor_result[24]);
  and and_57 (and_57_out, or_56_out, xor_result[24]);
  or or_57 (or_57_out, and_57_out, and_result[24]);
  xor xor_58 (add_result[25], or_57_out, xor_result[25]);
  and and_58 (and_58_out, or_57_out, xor_result[25]);
  or or_58 (or_58_out, and_58_out, and_result[25]);
  xor xor_59 (add_result[26], or_58_out, xor_result[26]);
  and and_59 (and_59_out, or_58_out, xor_result[26]);
  or or_59 (or_59_out, and_59_out, and_result[26]);
  xor xor_60 (add_result[27], or_59_out, xor_result[27]);
  and and_60 (and_60_out, or_59_out, xor_result[27]);
  or or_60 (or_60_out, and_60_out, and_result[27]);
  xor xor_61 (add_result[28], or_60_out, xor_result[28]);
  and and_61 (and_61_out, or_60_out, xor_result[28]);
  or or_61 (or_61_out, and_61_out, and_result[28]);
  xor xor_62 (add_result[29], or_61_out, xor_result[29]);
  and and_62 (and_62_out, or_61_out, xor_result[29]);
  or or_62 (or_62_out, and_62_out, and_result[29]);
  xor xor_63 (add_result[30], or_62_out, xor_result[30]);
  and and_63 (and_63_out, or_62_out, xor_result[30]);
  or or_63 (or_63_out, and_63_out, and_result[30]);
  xor xor_64 (add_result[31], or_63_out, xor_result[31]);
  and and_64 (and_64_out, or_63_out, xor_result[31]);
  or or_64 (carry, and_64_out, and_result[31]);
endmodule

module shift (
  input  [4:0] b,
  input  [31:0] a,
  input  right,
  input  arith,
  output [31:0] result
);

  wire and_2_out;
  wire [31:0] mux32_1_out_4, mux32_2_out_4, mux32_3_out_4, mux32_4_out_4, mux32_5_out_4, mux32_6_out_4;
  wire [31:31] and_1_out;

  and and_1 (and_1_out[31], a[31], and_2_out);
  and and_2 (and_2_out, right, arith);
  mux32 mux32_1 (
    .in_3({a[0], a[1], a[2], a[3], a[4], a[5], a[6], a[7], a[8], a[9], a[10], a[11], a[12], a[13], a[14], a[15], a[16], a[17], a[18], a[19], a[20], a[21], a[22], a[23], a[24], a[25], a[26], a[27], a[28], a[29], a[30], a[31]}),
    .in_2(a), .in_1(right), .out_4(mux32_1_out_4));
  mux32 mux32_2 (.in_3({and_1_out[31], mux32_1_out_4[31:1]}), .in_2(mux32_1_out_4), .in_1(b[0]), .out_4(mux32_2_out_4));
  mux32 mux32_3 (
    .in_3({{2{and_1_out[31]}}, mux32_2_out_4[31:2]}), .in_2(mux32_2_out_4), .in_1(b[1]), .out_4(mux32_3_out_4));
  mux32 mux32_4 (
    .in_3({{4{and_1_out[31]}}, mux32_3_out_4[31:4]}), .in_2(mux32_3_out_4), .in_1(b[2]), .out_4(mux32_4_out_4));
  mux32 mux32_5 (
    .in_3({{8{and_1_out[31]}}, mux32_4_out_4[31:8]}), .in_2(mux32_4_out_4), .in_1(b[3]), .out_4(mux32_5_out_4));
  mux32 mux32_6 (
    .in_3({{16{and_1_out[31]}}, mux32_5_out_4[31:16]}), .in_2(mux32_5_out_4), .in_1(b[4]),
    .out_4(mux32_6_out_4));
  mux32 mux32_7 (
    .in_3({mux32_6_out_4[0], mux32_6_out_4[1], mux32_6_out_4[2], mux32_6_out_4[3], mux32_6_out_4[4], mux32_6_out_4[5], mux32_6_out_4[6], mux32_6_out_4[7], mux32_6_out_4[8], mux32_6_out_4[9], mux32_6_out_4[10], mux32_6_out_4[11], mux32_6_out_4[12], mux32_6_out_4[13], mux32_6_out_4[14], mux32_6_out_4[15], mux32_6_out_4[16], mux32_6_out_4[17], mux32_6_out_4[18], mux32_6_out_4[19], mux32_6_out_4[20], mux32_6_out_4[21], mux32_6_out_4[22], mux32_6_out_4[23], mux32_6_out_4[24], mux32_6_out_4[25], mux32_6_out_4[26], mux32_6_out_4[27], mux32_6_out_4[28], mux32_6_out_4[29], mux32_6_out_4[30], mux32_6_out_4[31]}),
    .in_2(mux32_6_out_4), .in_1(right), .out_4(result));
endmodule

module opcode (
  input  [6:0] op,
  output error,
  output out_3,
  output out_4,
  output out_5,
  output out_6,
  output out_7,
  output out_8,
  output out_9,
  output out_10,
  output out_11,
  output out_12,
  output out_13
);

  wire and_1_out, and_2_out, and_3_out, and_4_out, and_5_out, and_6_out, and_7_out, and_8_out, and_9_out,
       and_10_out, and_11_out, and_12_out, and_13_out, and_14_out, and_15_out, and_16_out, and_17_out,
       and_18_out, and_19_out, and_20_out, and_21_out, and_22_out, and_23_out, and_24_out, and_25_out,
       and_26_out, and_27_out, not_1_out, not_2_out, not_3_out, not_4_out, not_5_out, not_6_out, not_7_out,
       not_8_out, not_9_out, not_10_out, not_11_out, not_12_out, not_13_out, not_14_out, not_15_out,
       or_1_out, or_2_out, or_3_out, or_4_out, or_6_out, or_7_out, or_8_out, or_9_out, or_10_out, or_11_out;

  not not_1 (not_1_out, and_1_out);
  and and_1 (and_1_out, op[0], op[1]);
  not not_2 (not_2_out, op[4]);
  not not_3 (not_3_out, op[5]);
  not not_4 (not_4_out, op[6]);
  not not_5 (not_5_out, op[4]);
  not not_6 (not_6_out, op[6]);
  not not_7 (not_7_out, op[6]);
  not not_8 (not_8_out, op[5]);
  not not_9 (not_9_out, op[6]);
  not not_10 (not_10_out, op[4]);
  not not_11 (not_11_out, op[3]);
  not not_12 (not_12_out, op[2]);
  and and_2 (and_2_out, not_11_out, not_12_out);
  and and_3 (and_3_out, not_2_out, not_3_out);
  and and_4 (and_4_out, and_3_out, not_4_out);
  and and_5 (and_5_out, not_5_out, op[5]);
  and and_6 (and_6_out, and_5_out, not_6_out);
  and and_7 (and_7_out, op[4], op[5]);
  and and_8 (and_8_out, and_7_out, not_7_out);
  and and_9 (and_9_out, op[4], not_8_out);
  and and_10 (and_10_out, and_9_out, not_9_out);
  and and_11 (and_11_out, not_10_out, op[5]);
  and and_12 (and_12_out, and_11_out, op[6]);
  and and_13 (and_13_out, op[4], op[5]);
  and and_14 (and_14_out, and_13_out, op[6]);
  not not_13 (not_13_out, op[3]);
  and and_15 (and_15_out, not_13_out, op[2]);
  and and_16 (and_16_out, op[3], op[2]);
  and and_17 (and_17_out, and_4_out, and_2_out);
  and and_18 (and_18_out, and_6_out, and_2_out);
  and and_19 (and_19_out, and_8_out, and_2_out);
  and and_20 (and_20_out, and_10_out, and_2_out);
  and and_21 (and_21_out, and_12_out, and_2_out);
  and and_22 (and_22_out, and_2_out, and_14_out);
  and and_23 (and_23_out, and_8_out, and_15_out);
  and and_24 (and_24_out, and_10_out, and_15_out);
  and and_25 (and_25_out, and_16_out, and_12_out);
  and and_26 (and_26_out, and_15_out, and_12_out);
  and and_27 (and_27_out, and_16_out, and_4_out);
  or or_1 (or_1_out, and_17_out, and_18_out);
  or or_2 (or_2_out, and_19_out, and_20_out);
  or or_3 (or_3_out, and_21_out, and_23_out);
  or or_4 (or_4_out, or_1_out, or_2_out);
  or or_5 (error, not_1_out, not_14_out);
  or or_6 (or_6_out, and_24_out, and_25_out);
  or or_7 (or_7_out, and_26_out, and_27_out);
  or or_8 (or_8_out, or_3_out, or_6_out);
  or or_9 (or_9_out, or_10_out, or_11_out);
  or or_10 (or_10_out, or_4_out, or_8_out);
  not not_14 (not_14_out, or_9_out);
  not not_15 (not_15_out, error);
  and and_28 (out_3, not_15_out, and_17_out);
  and and_29 (out_4, not_15_out, and_18_out);
  and and_30 (out_5, not_15_out, and_19_out);
  and and_31 (out_6, not_15_out, and_20_out);
  and and_32 (out_7, not_15_out, and_21_out);
  and and_33 (out_8, not_15_out, and_23_out);
  and and_34 (out_9, not_15_out, and_24_out);
  and and_35 (out_10, not_15_out, and_25_out);
  and and_36 (out_11, not_15_out, and_26_out);
  and and_37 (out_12, not_15_out, and_27_out);
  and and_38 (out_13, not_15_out, and_22_out);
  or or_11 (or_11_out, or_7_out, and_22_out);
endmodule

module imm (
  input  I,
  input  S,
  input  B,
  input  U,
  input  J,
  input  [4:0] in_6,
  input  [2:0] in_7,
  input  [4:0] in_8,
  input  [4:0] in_9,
  input  [6:0] in_10,
  output [31:0] result
);

  wire [31:0] mux32_1_out_4, mux32_2_out_4, mux32_3_out_4, mux32_4_out_4;

  mux32 mux32_1 (.in_3({{21{in_10[6]}}, in_10[5:0], in_9}), .in_2({32{1'b0}}), .in_1(I), .out_4(mux32_1_out_4));
  mux32 mux32_2 (.in_3({{21{in_10[6]}}, in_10[5:0], in_6}), .in_2(mux32_1_out_4), .in_1(S), .out_4(mux32_2_out_4));
  mux32 mux32_3 (
    .in_3({{20{in_10[6]}}, in_6[0], in_10[5:0], in_6[4:1], 1'b0}), .in_2(mux32_2_out_4), .in_1(B),
    .out_4(mux32_3_out_4));
  mux32 mux32_4 (.in_3({in_10, in_9, in_8, in_7, {12{1'b0}}}), .in_2(mux32_3_out_4), .in_1(U), .out_4(mux32_4_out_4));
  mux32 mux32_5 (
    .in_3({{12{in_10[6]}}, in_8, in_7, in_9[0], in_10[5:0], in_9[4:1], 1'b0}), .in_2(mux32_4_out_4),
    .in_1(J), .out_4(result));
endmodule

module add_er (
  input  [31:0] A,
  input  [31:0] B,
  output [31:0] result
);

  wire nand_1_out, nand_2_out, nand_3_out, nand_4_out, nand_5_out, nand_6_out, nand_7_out, nand_8_out,
       nand_9_out, nand_10_out, nand_11_out, nand_12_out, nand_13_out, nand_14_out, nand_15_out, nand_16_out,
       nand_17_out, nand_18_out, nand_19_out, nand_20_out, nand_21_out, nand_22_out, nand_23_out,
       nand_24_out, nand_25_out, nand_26_out, nand_27_out, nand_28_out, nand_29_out, nand_30_out,
       nand_31_out, nand_32_out, nand_33_out, nand_34_out, nand_35_out, nand_36_out, nand_37_out,
       nand_38_out, nand_39_out, nand_40_out, nand_41_out, nand_42_out, nand_43_out, nand_44_out,
       nand_45_out, nand_46_out, nand_47_out, nand_48_out, nand_49_out, nand_50_out, nand_51_out,
       nand_52_out, nand_53_out, nand_54_out, nand_55_out, nand_56_out, nand_57_out, nand_58_out,
       nand_59_out, nand_60_out, nand_61_out, nand_62_out, nand_63_out, nand_64_out, nand_65_out,
       nand_66_out, nand_67_out, nand_68_out, nand_69_out, nand_70_out, nand_71_out, nand_72_out,
       nand_73_out, nand_74_out, nand_75_out, nand_76_out, nand_77_out, nand_78_out, nand_79_out,
       nand_80_out, nand_81_out, nand_82_out, nand_83_out, nand_84_out, nand_85_out, nand_86_out,
       nand_87_out, nand_88_out, nand_89_out, nand_90_out, nand_91_out, nand_92_out, nand_93_out,
       nand_94_out, nand_95_out, nand_96_out, nand_98_out, nand_99_out, nand_100_out, nand_101_out,
       nand_102_out, nand_103_out, nand_104_out, nand_105_out, nand_106_out, nand_107_out, nand_108_out,
       nand_109_out, nand_110_out, nand_111_out, nand_112_out, nand_113_out, nand_114_out, nand_115_out,
       nand_116_out, nand_117_out, nand_118_out, nand_119_out, nand_120_out, nand_121_out, nand_122_out,
       nand_123_out, nand_124_out, nand_125_out, nand_126_out, nand_127_out, nand_128_out, nand_129_out,
       nand_130_out, nand_131_out, nand_132_out, nand_133_out, nand_134_out, nand_135_out, nand_136_out,
       nand_137_out, nand_138_out, nand_139_out, nand_140_out, nand_141_out, nand_142_out, nand_143_out,
       nand_144_out, nand_145_out, nand_146_out, nand_147_out, nand_148_out, nand_149_out, nand_150_out,
       nand_151_out, nand_152_out, nand_153_out, nand_154_out, nand_155_out, nand_156_out, nand_157_out,
       nand_158_out, nand_159_out, nand_160_out, nand_161_out, nand_162_out, nand_163_out, nand_164_out,
       nand_165_out, nand_166_out, nand_167_out, nand_168_out, nand_169_out, nand_170_out, nand_171_out,
       nand_172_out, nand_173_out, nand_174_out, nand_175_out, nand_176_out, nand_177_out, nand_178_out,
       nand_179_out, nand_180_out, nand_181_out, nand_182_out, nand_183_out, nand_184_out, nand_185_out,
       nand_186_out, nand_187_out, nand_188_out, nand_189_out, nand_190_out, nand_191_out, nand_192_out,
       nand_193_out, nand_194_out, nand_195_out, nand_196_out, nand_197_out, nand_198_out, nand_199_out,
       nand_200_out, nand_201_out, nand_202_out, nand_203_out, nand_204_out, nand_205_out, nand_206_out,
       nand_207_out, nand_208_out, nand_209_out, nand_210_out, nand_211_out, nand_212_out, nand_213_out,
       nand_214_out, nand_215_out, nand_216_out, nand_217_out, nand_218_out, nand_219_out, nand_220_out,
       nand_221_out, nand_222_out, nand_223_out, nand_224_out, nand_225_out, nand_226_out, nand_227_out,
       nand_228_out, nand_229_out, nand_230_out, nand_231_out, nand_232_out, nand_233_out, nand_234_out,
       nand_235_out, nand_236_out, nand_237_out, nand_238_out, nand_239_out, nand_240_out, nand_241_out,
       nand_242_out, nand_243_out, nand_244_out, nand_245_out, nand_246_out, nand_247_out, nand_248_out,
       nand_249_out, nand_250_out, nand_251_out, nand_252_out;

  nand nand_1 (nand_1_out, A[0], B[0]);
  nand nand_2 (nand_2_out, A[1], B[1]);
  nand nand_3 (nand_3_out, A[2], B[2]);
  nand nand_4 (nand_4_out, A[3], B[3]);
  nand nand_5 (nand_5_out, A[4], B[4]);
  nand nand_6 (nand_6_out, A[5], B[5]);
  nand nand_7 (nand_7_out, A[6], B[6]);
  nand nand_8 (nand_8_out, A[7], B[7]);
  nand nand_9 (nand_9_out, A[8], B[8]);
  nand nand_10 (nand_10_out, A[9], B[9]);
  nand nand_11 (nand_11_out, A[10], B[10]);
  nand nand_12 (nand_12_out, A[11], B[11]);
  nand nand_13 (nand_13_out, A[12], B[12]);
  nand nand_14 (nand_14_out, A[13], B[13]);
  nand nand_15 (nand_15_out, A[14], B[14]);
  nand nand_16 (nand_16_out, A[15], B[15]);
  nand nand_17 (nand_17_out, A[16], B[16]);
  nand nand_18 (nand_18_out, A[17], B[17]);
  nand nand_19 (nand_19_out, A[18], B[18]);
  nand nand_20 (nand_20_out, A[19], B[19]);
  nand nand_21 (nand_21_out, A[20], B[20]);
  nand nand_22 (nand_22_out, A[21], B[21]);
  nand nand_23 (nand_23_out, A[22], B[22]);
  nand nand_24 (nand_24_out, A[23], B[23]);
  nand nand_25 (nand_25_out, A[24], B[24]);
  nand nand_26 (nand_26_out, A[25], B[25]);
  nand nand_27 (nand_27_out, A[26], B[26]);
  nand nand_28 (nand_28_out, A[27], B[27]);
  nand nand_29 (nand_29_out, A[28], B[28]);
  nand nand_30 (nand_30_out, A[29], B[29]);
  nand nand_31 (nand_31_out, A[30], B[30]);
  nand nand_32 (nand_32_out, A[31], B[31]);
  nand nand_33 (nand_33_out, A[0], nand_1_out);
  nand nand_34 (nand_34_out, nand_1_out, B[0]);
  nand nand_35 (nand_35_out, A[1], nand_2_out);
  nand nand_36 (nand_36_out, nand_2_out, B[1]);
  nand nand_37 (nand_37_out, A[2], nand_3_out);
  nand nand_38 (nand_38_out, nand_3_out, B[2]);
  nand nand_39 (nand_39_out, A[3], nand_4_out);
  nand nand_40 (nand_40_out, nand_4_out, B[3]);
  nand nand_41 (nand_41_out, A[4], nand_5_out);
  nand nand_42 (nand_42_out, nand_5_out, B[4]);
  nand nand_43 (nand_43_out, A[5], nand_6_out);
  nand nand_44 (nand_44_out, nand_6_out, B[5]);
  nand nand_45 (nand_45_out, A[6], nand_7_out);
  nand nand_46 (nand_46_out, nand_7_out, B[6]);
  nand nand_47 (nand_47_out, A[7], nand_8_out);
  nand nand_48 (nand_48_out, nand_8_out, B[7]);
  nand nand_49 (nand_49_out, A[8], nand_9_out);
  nand nand_50 (nand_50_out, nand_9_out, B[8]);
  nand nand_51 (nand_51_out, A[9], nand_10_out);
  nand nand_52 (nand_52_out, nand_10_out, B[9]);
  nand nand_53 (nand_53_out, A[10], nand_11_out);
  nand nand_54 (nand_54_out, nand_11_out, B[10]);
  nand nand_55 (nand_55_out, A[11], nand_12_out);
  nand nand_56 (nand_56_out, nand_12_out, B[11]);
  nand nand_57 (nand_57_out, A[12], nand_13_out);
  nand nand_58 (nand_58_out, nand_13_out, B[12]);
  nand nand_59 (nand_59_out, A[13], nand_14_out);
  nand nand_60 (nand_60_out, nand_14_out, B[13]);
  nand nand_61 (nand_61_out, A[14], nand_15_out);
  nand nand_62 (nand_62_out, nand_15_out, B[14]);
  nand nand_63 (nand_63_out, A[15], nand_16_out);
  nand nand_64 (nand_64_out, nand_16_out, B[15]);
  nand nand_65 (nand_65_out, A[16], nand_17_out);
  nand nand_66 (nand_66_out, nand_17_out, B[16]);
  nand nand_67 (nand_67_out, A[17], nand_18_out);
  nand nand_68 (nand_68_out, nand_18_out, B[17]);
  nand nand_69 (nand_69_out, A[18], nand_19_out);
  nand nand_70 (nand_70_out, nand_19_out, B[18]);
  nand nand_71 (nand_71_out, A[19], nand_20_out);
  nand nand_72 (nand_72_out, nand_20_out, B[19]);
  nand nand_73 (nand_73_out, A[20], nand_21_out);
  nand nand_74 (nand_74_out, nand_21_out, B[20]);
  nand nand_75 (nand_75_out, A[21], nand_22_out);
  nand nand_76 (nand_76_out, nand_22_out, B[21]);
  nand nand_77 (nand_77_out, A[22], nand_23_out);
  nand nand_78 (nand_78_out, nand_23_out, B[22]);
  nand nand_79 (nand_79_out, A[23], nand_24_out);
  nand nand_80 (nand_80_out, nand_24_out, B[23]);
  nand nand_81 (nand_81_out, A[24], nand_25_out);
  nand nand_82 (nand_82_out, nand_25_out, B[24]);
  nand nand_83 (nand_83_out, A[25], nand_26_out);
  nand nand_84 (nand_84_out, nand_26_out, B[25]);
  nand nand_85 (nand_85_out, A[26], nand_27_out);
  nand nand_86 (nand_86_out, nand_27_out, B[26]);
  nand nand_87 (nand_87_out, A[27], nand_28_out);
  nand nand_88 (nand_88_out, nand_28_out, B[27]);
  nand nand_89 (nand_89_out, A[28], nand_29_out);
  nand nand_90 (nand_90_out, nand_29_out, B[28]);
  nand nand_91 (nand_91_out, A[29], nand_30_out);
  nand nand_92 (nand_92_out, nand_30_out, B[29]);
  nand nand_93 (nand_93_out, A[30], nand_31_out);
  nand nand_94 (nand_94_out, nand_31_out, B[30]);
  nand nand_95 (nand_95_out, A[31], nand_32_out);
  nand nand_96 (nand_96_out, nand_32_out, B[31]);
  nand nand_97 (result[0], nand_33_out, nand_34_out);
  nand nand_98 (nand_98_out, nand_1_out, nand_1_out);
  nand nand_99 (nand_99_out, nand_98_out, nand_100_out);
  nand nand_100 (nand_100_out, nand_35_out, nand_36_out);
  nand nand_101 (nand_101_out, nand_99_out, nand_2_out);
  nand nand_102 (nand_102_out, nand_101_out, nand_103_out);
  nand nand_103 (nand_103_out, nand_37_out, nand_38_out);
  nand nand_104 (nand_104_out, nand_102_out, nand_3_out);
  nand nand_105 (nand_105_out, nand_104_out, nand_106_out);
  nand nand_106 (nand_106_out, nand_39_out, nand_40_out);
  nand nand_107 (nand_107_out, nand_105_out, nand_4_out);
  nand nand_108 (nand_108_out, nand_107_out, nand_109_out);
  nand nand_109 (nand_109_out, nand_41_out, nand_42_out);
  nand nand_110 (nand_110_out, nand_108_out, nand_5_out);
  nand nand_111 (nand_111_out, nand_110_out, nand_112_out);
  nand nand_112 (nand_112_out, nand_43_out, nand_44_out);
  nand nand_113 (nand_113_out, nand_111_out, nand_6_out);
  nand nand_114 (nand_114_out, nand_113_out, nand_115_out);
  nand nand_115 (nand_115_out, nand_45_out, nand_46_out);
  nand nand_116 (nand_116_out, nand_114_out, nand_7_out);
  nand nand_117 (nand_117_out, nand_116_out, nand_118_out);
  nand nand_118 (nand_118_out, nand_47_out, nand_48_out);
  nand nand_119 (nand_119_out, nand_117_out, nand_8_out);
  nand nand_120 (nand_120_out, nand_119_out, nand_121_out);
  nand nand_121 (nand_121_out, nand_49_out, nand_50_out);
  nand nand_122 (nand_122_out, nand_120_out, nand_9_out);
  nand nand_123 (nand_123_out, nand_122_out, nand_124_out);
  nand nand_124 (nand_124_out, nand_51_out, nand_52_out);
  nand nand_125 (nand_125_out, nand_123_out, nand_10_out);
  nand nand_126 (nand_126_out, nand_125_out, nand_127_out);
  nand nand_127 (nand_127_out, nand_53_out, nand_54_out);
  nand nand_128 (nand_128_out, nand_126_out, nand_11_out);
  nand nand_129 (nand_129_out, nand_128_out, nand_130_out);
  nand nand_130 (nand_130_out, nand_55_out, nand_56_out);
  nand nand_131 (nand_131_out, nand_129_out, nand_12_out);
  nand nand_132 (nand_132_out, nand_131_out, nand_133_out);
  nand nand_133 (nand_133_out, nand_57_out, nand_58_out);
  nand nand_134 (nand_134_out, nand_132_out, nand_13_out);
  nand nand_135 (nand_135_out, nand_134_out, nand_136_out);
  nand nand_136 (nand_136_out, nand_59_out, nand_60_out);
  nand nand_137 (nand_137_out, nand_135_out, nand_14_out);
  nand nand_138 (nand_138_out, nand_137_out, nand_139_out);
  nand nand_139 (nand_139_out, nand_61_out, nand_62_out);
  nand nand_140 (nand_140_out, nand_138_out, nand_15_out);
  nand nand_141 (nand_141_out, nand_140_out, nand_142_out);
  nand nand_142 (nand_142_out, nand_63_out, nand_64_out);
  nand nand_143 (nand_143_out, nand_141_out, nand_16_out);
  nand nand_144 (nand_144_out, nand_143_out, nand_145_out);
  nand nand_145 (nand_145_out, nand_65_out, nand_66_out);
  nand nand_146 (nand_146_out, nand_144_out, nand_17_out);
  nand nand_147 (nand_147_out, nand_146_out, nand_148_out);
  nand nand_148 (nand_148_out, nand_67_out, nand_68_out);
  nand nand_149 (nand_149_out, nand_147_out, nand_18_out);
  nand nand_150 (nand_150_out, nand_149_out, nand_151_out);
  nand nand_151 (nand_151_out, nand_69_out, nand_70_out);
  nand nand_152 (nand_152_out, nand_150_out, nand_19_out);
  nand nand_153 (nand_153_out, nand_152_out, nand_154_out);
  nand nand_154 (nand_154_out, nand_71_out, nand_72_out);
  nand nand_155 (nand_155_out, nand_153_out, nand_20_out);
  nand nand_156 (nand_156_out, nand_155_out, nand_157_out);
  nand nand_157 (nand_157_out, nand_73_out, nand_74_out);
  nand nand_158 (nand_158_out, nand_156_out, nand_21_out);
  nand nand_159 (nand_159_out, nand_158_out, nand_160_out);
  nand nand_160 (nand_160_out, nand_75_out, nand_76_out);
  nand nand_161 (nand_161_out, nand_159_out, nand_22_out);
  nand nand_162 (nand_162_out, nand_161_out, nand_163_out);
  nand nand_163 (nand_163_out, nand_77_out, nand_78_out);
  nand nand_164 (nand_164_out, nand_162_out, nand_23_out);
  nand nand_165 (nand_165_out, nand_164_out, nand_166_out);
  nand nand_166 (nand_166_out, nand_79_out, nand_80_out);
  nand nand_167 (nand_167_out, nand_165_out, nand_24_out);
  nand nand_168 (nand_168_out, nand_167_out, nand_169_out);
  nand nand_169 (nand_169_out, nand_81_out, nand_82_out);
  nand nand_170 (nand_170_out, nand_168_out, nand_25_out);
  nand nand_171 (nand_171_out, nand_170_out, nand_172_out);
  nand nand_172 (nand_172_out, nand_83_out, nand_84_out);
  nand nand_173 (nand_173_out, nand_171_out, nand_26_out);
  nand nand_174 (nand_174_out, nand_173_out, nand_175_out);
  nand nand_175 (nand_175_out, nand_85_out, nand_86_out);
  nand nand_176 (nand_176_out, nand_174_out, nand_27_out);
  nand nand_177 (nand_177_out, nand_176_out, nand_178_out);
  nand nand_178 (nand_178_out, nand_87_out, nand_88_out);
  nand nand_179 (nand_179_out, nand_177_out, nand_28_out);
  nand nand_180 (nand_180_out, nand_179_out, nand_181_out);
  nand nand_181 (nand_181_out, nand_89_out, nand_90_out);
  nand nand_182 (nand_182_out, nand_180_out, nand_29_out);
  nand nand_183 (nand_183_out, nand_182_out, nand_184_out);
  nand nand_184 (nand_184_out, nand_91_out, nand_92_out);
  nand nand_185 (nand_185_out, nand_183_out, nand_30_out);
  nand nand_186 (nand_186_out, nand_185_out, nand_187_out);
  nand nand_187 (nand_187_out, nand_93_out, nand_94_out);
  nand nand_188 (nand_188_out, nand_186_out, nand_31_out);
  nand nand_189 (nand_189_out, nand_188_out, nand_190_out);
  nand nand_190 (nand_190_out, nand_95_out, nand_96_out);
  nand nand_191 (nand_191_out, nand_98_out, nand_99_out);
  nand nand_192 (nand_192_out, nand_99_out, nand_100_out);
  nand nand_193 (nand_193_out, nand_101_out, nand_102_out);
  nand nand_194 (nand_194_out, nand_102_out, nand_103_out);
  nand nand_195 (nand_195_out, nand_104_out, nand_105_out);
  nand nand_196 (nand_196_out, nand_105_out, nand_106_out);
  nand nand_197 (nand_197_out, nand_107_out, nand_108_out);
  nand nand_198 (nand_198_out, nand_108_out, nand_109_out);
  nand nand_199 (nand_199_out, nand_110_out, nand_111_out);
  nand nand_200 (nand_200_out, nand_111_out, nand_112_out);
  nand nand_201 (nand_201_out, nand_113_out, nand_114_out);
  nand nand_202 (nand_202_out, nand_114_out, nand_115_out);
  nand nand_203 (nand_203_out, nand_116_out, nand_117_out);
  nand nand_204 (nand_204_out, nand_117_out, nand_118_out);
  nand nand_205 (nand_205_out, nand_119_out, nand_120_out);
  nand nand_206 (nand_206_out, nand_120_out, nand_121_out);
  nand nand_207 (nand_207_out, nand_122_out, nand_123_out);
  nand nand_208 (nand_208_out, nand_123_out, nand_124_out);
  nand nand_209 (nand_209_out, nand_125_out, nand_126_out);
  nand nand_210 (nand_210_out, nand_126_out, nand_127_out);
  nand nand_211 (nand_211_out, nand_128_out, nand_129_out);
  nand nand_212 (nand_212_out, nand_129_out, nand_130_out);
  nand nand_213 (nand_213_out, nand_131_out, nand_132_out);
  nand nand_214 (nand_214_out, nand_132_out, nand_133_out);
  nand nand_215 (nand_215_out, nand_134_out, nand_135_out);
  nand nand_216 (nand_216_out, nand_135_out, nand_136_out);
  nand nand_217 (nand_217_out, nand_137_out, nand_138_out);
  nand nand_218 (nand_218_out, nand_138_out, nand_139_out);
  nand nand_219 (nand_219_out, nand_140_out, nand_141_out);
  nand nand_220 (nand_220_out, nand_141_out, nand_142_out);
  nand nand_221 (nand_221_out, nand_143_out, nand_144_out);
  nand nand_222 (nand_222_out, nand_144_out, nand_145_out);
  nand nand_223 (nand_223_out, nand_146_out, nand_147_out);
  nand nand_224 (nand_224_out, nand_147_out, nand_148_out);
  nand nand_225 (nand_225_out, nand_149_out, nand_150_out);
  nand nand_226 (nand_226_out, nand_150_out, nand_151_out);
  nand nand_227 (nand_227_out, nand_152_out, nand_153_out);
  nand nand_228 (nand_228_out, nand_153_out, nand_154_out);
  nand nand_229 (nand_229_out, nand_155_out, nand_156_out);
  nand nand_230 (nand_230_out, nand_156_out, nand_157_out);
  nand nand_231 (nand_231_out, nand_158_out, nand_159_out);
  nand nand_232 (nand_232_out, nand_159_out, nand_160_out);
  nand nand_233 (nand_233_out, nand_161_out, nand_162_out);
  nand nand_234 (nand_234_out, nand_162_out, nand_163_out);
  nand nand_235 (nand_235_out, nand_164_out, nand_165_out);
  nand nand_236 (nand_236_out, nand_165_out, nand_166_out);
  nand nand_237 (nand_237_out, nand_167_out, nand_168_out);
  nand nand_238 (nand_238_out, nand_168_out, nand_169_out);
  nand nand_239 (nand_239_out, nand_170_out, nand_171_out);
  nand nand_240 (nand_240_out, nand_171_out, nand_172_out);
  nand nand_241 (nand_241_out, nand_173_out, nand_174_out);
  nand nand_242 (nand_242_out, nand_174_out, nand_175_out);
  nand nand_243 (nand_243_out, nand_176_out, nand_177_out);
  nand nand_244 (nand_244_out, nand_177_out, nand_178_out);
  nand nand_245 (nand_245_out, nand_179_out, nand_180_out);
  nand nand_246 (nand_246_out, nand_180_out, nand_181_out);
  nand nand_247 (nand_247_out, nand_182_out, nand_183_out);
  nand nand_248 (nand_248_out, nand_183_out, nand_184_out);
  nand nand_249 (nand_249_out, nand_185_out, nand_186_out);
  nand nand_250 (nand_250_out, nand_186_out, nand_187_out);
  nand nand_251 (nand_251_out, nand_188_out, nand_189_out);
  nand nand_252 (nand_252_out, nand_189_out, nand_190_out);
  nand nand_253 (result[1], nand_191_out, nand_192_out);
  nand nand_254 (result[2], nand_193_out, nand_194_out);
  nand nand_255 (result[3], nand_195_out, nand_196_out);
  nand nand_256 (result[4], nand_197_out, nand_198_out);
  nand nand_257 (result[5], nand_199_out, nand_200_out);
  nand nand_258 (result[6], nand_201_out, nand_202_out);
  nand nand_259 (result[7], nand_203_out, nand_204_out);
  nand nand_260 (result[8], nand_205_out, nand_206_out);
  nand nand_261 (result[9], nand_207_out, nand_208_out);
  nand nand_262 (result[10], nand_209_out, nand_210_out);
  nand nand_263 (result[11], nand_211_out, nand_212_out);
  nand nand_264 (result[12], nand_213_out, nand_214_out);
  nand nand_265 (result[13], nand_215_out, nand_216_out);
  nand nand_266 (result[14], nand_217_out, nand_218_out);
  nand nand_267 (result[15], nand_219_out, nand_220_out);
  nand nand_268 (result[16], nand_221_out, nand_222_out);
  nand nand_269 (result[17], nand_223_out, nand_224_out);
  nand nand_270 (result[18], nand_225_out, nand_226_out);
  nand nand_271 (result[19], nand_227_out, nand_228_out);
  nand nand_272 (result[20], nand_229_out, nand_230_out);
  nand nand_273 (result[21], nand_231_out, nand_232_out);
  nand nand_274 (result[22], nand_233_out, nand_234_out);
  nand nand_275 (result[23], nand_235_out, nand_236_out);
  nand nand_276 (result[24], nand_237_out, nand_238_out);
  nand nand_277 (result[25], nand_239_out, nand_240_out);
  nand nand_278 (result[26], nand_241_out, nand_242_out);
  nand nand_279 (result[27], nand_243_out, nand_244_out);
  nand nand_280 (result[28], nand_245_out, nand_246_out);
  nand nand_281 (result[29], nand_247_out, nand_248_out);
  nand nand_282 (result[30], nand_249_out, nand_250_out);
  nand nand_283 (result[31], nand_251_out, nand_252_out);
endmodule

module op_to_ALU (
  input  in_1,
  input  in_2,
  input  in_3,
  input  in_4,
  input  in_5,
  input  in_6,
  input  in_7,
  input  in_8,
  input  in_9,
  input  in_10,
  input  in_11,
  input  in_12,
  input  [2:0] in_13,
  output error,
  output out_15,
  output out_16,
  output out_17,
  output out_18,
  output out_19,
  output out_20
);

  wire and_1_out, and_2_out, and_3_out, and_4_out, and_5_out, and_6_out, and_7_out, and_8_out, and_9_out,
       and_10_out, and_11_out, and_12_out, and_13_out, and_14_out, and_15_out, and_16_out, and_17_out,
       and_18_out, and_19_out, and_20_out, and_21_out, and_22_out, and_23_out, and_24_out, and_25_out,
       and_26_out, and_27_out, and_28_out, and_29_out, and_30_out, and_31_out, and_32_out, and_33_out,
       and_34_out, and_35_out, and_36_out, and_37_out, and_38_out, and_39_out, and_40_out, and_41_out,
       and_42_out, and_43_out, and_44_out, and_45_out, and_46_out, and_47_out, and_48_out, and_49_out,
       and_50_out, and_51_out, not_1_out, not_2_out, not_3_out, not_4_out, not_5_out, not_6_out, not_7_out,
       not_8_out, not_9_out, not_10_out, not_11_out, not_12_out, not_13_out, or_1_out, or_2_out, or_3_out,
       or_4_out, or_5_out, or_6_out, or_7_out, or_8_out, or_9_out, or_10_out, or_11_out, or_12_out,
       or_13_out, or_14_out, or_15_out, or_16_out, or_17_out, or_18_out, or_19_out, or_20_out, or_21_out,
       or_22_out, or_24_out, or_25_out, or_26_out, or_27_out, or_28_out, or_29_out, or_30_out, or_31_out,
       or_32_out, or_33_out, or_34_out, or_35_out, or_37_out, or_38_out, or_40_out, or_42_out, or_43_out;

  or or_1 (or_1_out, or_2_out, and_40_out);
  or or_2 (or_2_out, and_3_out, and_5_out);
  and and_1 (and_1_out, or_3_out, in_1);
  and and_2 (and_2_out, or_1_out, in_2);
  not not_1 (not_1_out, in_12);
  or or_3 (or_3_out, or_1_out, or_4_out);
  or or_4 (or_4_out, and_44_out, and_46_out);
  and and_3 (and_3_out, and_4_out, not_4_out);
  and and_4 (and_4_out, not_2_out, not_3_out);
  not not_2 (not_2_out, in_13[0]);
  not not_3 (not_3_out, in_13[1]);
  not not_4 (not_4_out, in_13[2]);
  or or_5 (or_5_out, and_3_out, and_5_out);
  or or_6 (or_6_out, and_44_out, and_46_out);
  and and_5 (and_5_out, and_6_out, not_6_out);
  and and_6 (and_6_out, in_13[0], not_5_out);
  and and_7 (and_7_out, not_7_out, in_13[1]);
  not not_5 (not_5_out, in_13[1]);
  not not_6 (not_6_out, in_13[2]);
  not not_7 (not_7_out, in_13[0]);
  and and_8 (and_8_out, not_1_out, and_9_out);
  and and_9 (and_9_out, in_3, and_3_out);
  and and_10 (and_10_out, and_9_out, in_12);
  and and_11 (and_11_out, in_3, and_5_out);
  and and_12 (and_12_out, not_1_out, and_11_out);
  and and_13 (and_13_out, not_1_out, and_14_out);
  and and_14 (and_14_out, in_3, and_40_out);
  and and_15 (and_15_out, not_1_out, and_16_out);
  and and_16 (and_16_out, in_3, and_41_out);
  and and_17 (and_17_out, not_1_out, and_18_out);
  and and_18 (and_18_out, in_3, and_44_out);
  and and_19 (and_19_out, not_1_out, and_20_out);
  and and_20 (and_20_out, in_3, and_46_out);
  and and_21 (and_21_out, and_20_out, in_12);
  and and_22 (and_22_out, in_3, and_49_out);
  and and_23 (and_23_out, and_22_out, not_1_out);
  and and_24 (and_24_out, in_3, and_50_out);
  and and_25 (and_25_out, and_24_out, not_1_out);
  and and_26 (and_26_out, in_4, and_3_out);
  and and_27 (and_27_out, in_4, and_5_out);
  and and_28 (and_28_out, and_27_out, in_12);
  and and_29 (and_29_out, in_4, and_40_out);
  and and_30 (and_30_out, in_4, and_41_out);
  and and_31 (and_31_out, in_4, and_44_out);
  and and_32 (and_32_out, not_1_out, and_33_out);
  and and_33 (and_33_out, in_4, and_46_out);
  and and_34 (and_34_out, and_33_out, in_12);
  and and_35 (and_35_out, in_4, and_49_out);
  and and_36 (and_36_out, in_4, and_49_out);
  and and_37 (and_37_out, in_5, or_10_out);
  and and_38 (and_38_out, in_5, or_9_out);
  or or_7 (or_7_out, in_7, in_8);
  and and_39 (and_39_out, not_1_out, or_8_out);
  or or_8 (or_8_out, in_10, in_11);
  or or_9 (or_9_out, and_50_out, and_49_out);
  or or_10 (or_10_out, or_5_out, or_6_out);
  and and_40 (and_40_out, and_7_out, not_8_out);
  and and_41 (and_41_out, and_42_out, not_9_out);
  and and_42 (and_42_out, in_13[0], in_13[1]);
  not not_8 (not_8_out, in_13[2]);
  and and_43 (and_43_out, and_3_out, or_11_out);
  or or_11 (or_11_out, in_9, and_39_out);
  and and_44 (and_44_out, and_45_out, in_13[2]);
  and and_45 (and_45_out, not_10_out, not_11_out);
  not not_9 (not_9_out, in_13[2]);
  not not_10 (not_10_out, in_13[0]);
  not not_11 (not_11_out, in_13[1]);
  or or_12 (or_12_out, or_7_out, and_1_out);
  or or_13 (or_13_out, or_12_out, and_2_out);
  or or_14 (or_14_out, and_8_out, or_15_out);
  or or_15 (or_15_out, and_26_out, and_43_out);
  or or_16 (or_16_out, and_25_out, and_36_out);
  or or_17 (or_17_out, and_23_out, and_35_out);
  or or_18 (or_18_out, and_12_out, and_29_out);
  or or_19 (or_19_out, and_19_out, and_30_out);
  or or_20 (or_20_out, and_21_out, and_28_out);
  or or_21 (or_21_out, and_32_out, and_13_out);
  or or_22 (or_22_out, and_15_out, and_34_out);
  or or_23 (out_19, in_6, or_26_out);
  and and_46 (and_46_out, and_47_out, in_13[2]);
  and and_47 (and_47_out, in_13[0], not_12_out);
  and and_48 (and_48_out, not_13_out, in_13[1]);
  not not_12 (not_12_out, in_13[1]);
  not not_13 (not_13_out, in_13[0]);
  or or_24 (or_24_out, or_13_out, or_14_out);
  or or_25 (or_25_out, or_16_out, or_17_out);
  or or_26 (or_26_out, and_17_out, and_31_out);
  or or_27 (or_27_out, or_18_out, or_19_out);
  or or_28 (or_28_out, or_21_out, and_37_out);
  or or_29 (or_29_out, or_22_out, and_38_out);
  and and_49 (and_49_out, and_48_out, in_13[2]);
  and and_50 (and_50_out, and_51_out, in_13[2]);
  and and_51 (and_51_out, in_13[0], in_13[1]);
  or or_30 (or_30_out, or_24_out, and_10_out);
  or or_31 (or_31_out, or_25_out, or_32_out);
  or or_32 (or_32_out, or_33_out, or_34_out);
  or or_33 (or_33_out, out_19, or_27_out);
  or or_34 (or_34_out, or_20_out, or_35_out);
  or or_35 (or_35_out, or_28_out, or_29_out);
  or or_36 (out_20, or_17_out, in_6);
  or or_37 (or_37_out, or_30_out, or_31_out);
  not not_14 (error, or_37_out);
  or or_38 (or_38_out, or_27_out, or_20_out);
  or or_39 (out_15, or_38_out, or_35_out);
  or or_40 (or_40_out, or_25_out, or_26_out);
  or or_41 (out_16, or_40_out, or_42_out);
  or or_42 (or_42_out, or_35_out, in_6);
  or or_43 (or_43_out, and_10_out, or_20_out);
  or or_44 (out_17, or_43_out, or_19_out);
  or or_45 (out_18, or_29_out, or_20_out);
endmodule

module comp (
  input  zero,
  input  neg,
  input  [2:0] f3,
  output true
);

  wire and_1_out, mux_1_out_4, not_1_out, not_2_out, not_3_out;

  not not_1 (not_1_out, f3[0]);
  mux mux_1 (.in_2(neg), .in_3(zero), .in_1(and_1_out), .out_4(mux_1_out_4));
  and and_1 (and_1_out, not_1_out, not_2_out);
  not not_2 (not_2_out, f3[1]);
  mux mux_2 (.in_2(mux_1_out_4), .in_3(not_3_out), .in_1(f3[2]), .out_4(true));
  not not_3 (not_3_out, mux_1_out_4);
endmodule

module bit32 (
  input  load,
  input  [31:0] in_2,
  output [31:0] out_3
);

  Clock clock_1 ();  // open: out
  \bit  bit_1 (.in_2(in_2[0]), .load(load), .out_3(out_3[0]));
  \bit  bit_2 (.in_2(in_2[1]), .load(load), .out_3(out_3[1]));
  \bit  bit_3 (.in_2(in_2[2]), .load(load), .out_3(out_3[2]));
  \bit  bit_4 (.in_2(in_2[3]), .load(load), .out_3(out_3[3]));
  \bit  bit_5 (.in_2(in_2[4]), .load(load), .out_3(out_3[4]));
  \bit  bit_6 (.in_2(in_2[5]), .load(load), .out_3(out_3[5]));
  \bit  bit_7 (.in_2(in_2[6]), .load(load), .out_3(out_3[6]));
  \bit  bit_8 (.in_2(in_2[7]), .load(load), .out_3(out_3[7]));
  \bit  bit_9 (.in_2(in_2[8]), .load(load), .out_3(out_3[8]));
  \bit  bit_10 (.in_2(in_2[9]), .load(load), .out_3(out_3[9]));
  \bit  bit_11 (.in_2(in_2[10]), .load(load), .out_3(out_3[10]));
  \bit  bit_12 (.in_2(in_2[11]), .load(load), .out_3(out_3[11]));
  \bit  bit_13 (.in_2(in_2[12]), .load(load), .out_3(out_3[12]));
  \bit  bit_14 (.in_2(in_2[13]), .load(load), .out_3(out_3[13]));
  \bit  bit_15 (.in_2(in_2[14]), .load(load), .out_3(out_3[14]));
  \bit  bit_16 (.in_2(in_2[15]), .load(load), .out_3(out_3[15]));
  \bit  bit_17 (.in_2(in_2[16]), .load(load), .out_3(out_3[16]));
  \bit  bit_18 (.in_2(in_2[17]), .load(load), .out_3(out_3[17]));
  \bit  bit_19 (.in_2(in_2[18]), .load(load), .out_3(out_3[18]));
  \bit  bit_20 (.in_2(in_2[19]), .load(load), .out_3(out_3[19]));
  \bit  bit_21 (.in_2(in_2[20]), .load(load), .out_3(out_3[20]));
  \bit  bit_22 (.in_2(in_2[21]), .load(load), .out_3(out_3[21]));
  \bit  bit_23 (.in_2(in_2[22]), .load(load), .out_3(out_3[22]));
  \bit  bit_24 (.in_2(in_2[23]), .load(load), .out_3(out_3[23]));
  \bit  bit_25 (.in_2(in_2[24]), .load(load), .out_3(out_3[24]));
  \bit  bit_26 (.in_2(in_2[25]), .load(load), .out_3(out_3[25]));
  \bit  bit_27 (.in_2(in_2[26]), .load(load), .out_3(out_3[26]));
  \bit  bit_28 (.in_2(in_2[27]), .load(load), .out_3(out_3[27]));
  \bit  bit_29 (.in_2(in_2[28]), .load(load), .out_3(out_3[28]));
  \bit  bit_30 (.in_2(in_2[29]), .load(load), .out_3(out_3[29]));
  \bit  bit_31 (.in_2(in_2[30]), .load(load), .out_3(out_3[30]));
  \bit  bit_32 (.in_2(in_2[31]), .load(load), .out_3(out_3[31]));
endmodule

module dmux32way (
  input  [4:0] in_1,
  input  in_2,
  output out_3,
  output out_4,
  output out_5,
  output out_6,
  output out_7,
  output out_8,
  output out_9,
  output out_10,
  output out_11,
  output out_12,
  output out_13,
  output out_14,
  output out_15,
  output out_16,
  output out_17,
  output out_18,
  output out_19,
  output out_20,
  output out_21,
  output out_22,
  output out_23,
  output out_24,
  output out_25,
  output out_26,
  output out_27,
  output out_28,
  output out_29,
  output out_30,
  output out_31,
  output out_32,
  output out_33,
  output out_34
);

  wire and_1_out, and_2_out, and_3_out, and_4_out, and_5_out, and_6_out, and_7_out, and_8_out, and_9_out,
       and_10_out, and_11_out, and_12_out, and_13_out, and_14_out, and_15_out, and_16_out, and_17_out,
       and_18_out, and_19_out, and_20_out, and_21_out, and_22_out, and_23_out, and_24_out, and_25_out,
       and_26_out, and_27_out, and_28_out, and_29_out, and_30_out, not_1_out, not_2_out, not_3_out,
       not_4_out, not_5_out;

  not not_1 (not_1_out, in_1[4]);
  and and_1 (and_1_out, not_1_out, in_2);
  and and_2 (and_2_out, in_1[4], in_2);
  not not_2 (not_2_out, in_1[3]);
  and and_3 (and_3_out, not_2_out, and_1_out);
  and and_4 (and_4_out, in_1[3], and_1_out);
  and and_5 (and_5_out, not_2_out, and_2_out);
  and and_6 (and_6_out, in_1[3], and_2_out);
  not not_3 (not_3_out, in_1[2]);
  and and_7 (and_7_out, not_3_out, and_3_out);
  and and_8 (and_8_out, in_1[2], and_3_out);
  and and_9 (and_9_out, not_3_out, and_4_out);
  and and_10 (and_10_out, in_1[2], and_4_out);
  and and_11 (and_11_out, not_3_out, and_5_out);
  and and_12 (and_12_out, in_1[2], and_5_out);
  and and_13 (and_13_out, not_3_out, and_6_out);
  and and_14 (and_14_out, in_1[2], and_6_out);
  not not_4 (not_4_out, in_1[1]);
  not not_5 (not_5_out, in_1[0]);
  and and_15 (and_15_out, not_4_out, and_7_out);
  and and_16 (and_16_out, in_1[1], and_7_out);
  and and_17 (and_17_out, not_4_out, and_8_out);
  and and_18 (and_18_out, in_1[1], and_8_out);
  and and_19 (and_19_out, not_4_out, and_9_out);
  and and_20 (and_20_out, in_1[1], and_9_out);
  and and_21 (and_21_out, not_4_out, and_10_out);
  and and_22 (and_22_out, in_1[1], and_10_out);
  and and_23 (and_23_out, not_4_out, and_11_out);
  and and_24 (and_24_out, in_1[1], and_11_out);
  and and_25 (and_25_out, not_4_out, and_12_out);
  and and_26 (and_26_out, in_1[1], and_12_out);
  and and_27 (and_27_out, not_4_out, and_13_out);
  and and_28 (and_28_out, in_1[1], and_13_out);
  and and_29 (and_29_out, not_4_out, and_14_out);
  and and_30 (and_30_out, in_1[1], and_14_out);
  and and_31 (out_3, not_5_out, and_15_out);
  and and_32 (out_4, in_1[0], and_15_out);
  and and_33 (out_5, not_5_out, and_16_out);
  and and_34 (out_6, in_1[0], and_16_out);
  and and_35 (out_7, not_5_out, and_17_out);
  and and_36 (out_8, in_1[0], and_17_out);
  and and_37 (out_9, not_5_out, and_18_out);
  and and_38 (out_10, in_1[0], and_18_out);
  and and_39 (out_11, not_5_out, and_19_out);
  and and_40 (out_12, in_1[0], and_19_out);
  and and_41 (out_13, not_5_out, and_20_out);
  and and_42 (out_14, in_1[0], and_20_out);
  and and_43 (out_15, not_5_out, and_21_out);
  and and_44 (out_16, in_1[0], and_21_out);
  and and_45 (out_17, not_5_out, and_22_out);
  and and_46 (out_18, in_1[0], and_22_out);
  and and_47 (out_19, not_5_out, and_23_out);
  and and_48 (out_20, in_1[0], and_23_out);
  and and_49 (out_21, not_5_out, and_24_out);
  and and_50 (out_22, in_1[0], and_24_out);
  and and_51 (out_23, not_5_out, and_25_out);
  and and_52 (out_24, in_1[0], and_25_out);
  and and_53 (out_25, not_5_out, and_26_out);
  and and_54 (out_26, in_1[0], and_26_out);
  and and_55 (out_27, not_5_out, and_27_out);
  and and_56 (out_28, in_1[0], and_27_out);
  and and_57 (out_29, not_5_out, and_28_out);
  and and_58 (out_30, in_1[0], and_28_out);
  and and_59 (out_31, not_5_out, and_29_out);
  and and_60 (out_32, in_1[0], and_29_out);
  and and_61 (out_33, not_5_out, and_30_out);
  and and_62 (out_34, in_1[0], and_30_out);
endmodule

module mux32bit32way (
  input  [4:0] in_1,
  input  [31:0] in_2,
  input  [31:0] in_3,
  input  [31:0] in_4,
  input  [31:0] in_5,
  input  [31:0] in_6,
  input  [31:0] in_7,
  input  [31:0] in_8,
  input  [31:0] in_9,
  input  [31:0] in_10,
  input  [31:0] in_11,
  input  [31:0] in_12,
  input  [31:0] in_13,
  input  [31:0] in_14,
  input  [31:0] in_15,
  input  [31:0] in_16,
  input  [31:0] in_17,
  input  [31:0] in_18,
  input  [31:0] in_19,
  input  [31:0] in_20,
  input  [31:0] in_21,
  input  [31:0] in_22,
  input  [31:0] in_23,
  input  [31:0] in_24,
  input  [31:0] in_25,
  input  [31:0] in_26,
  input  [31:0] in_27,
  input  [31:0] in_28,
  input  [31:0] in_29,
  input  [31:0] in_30,
  input  [31:0] in_31,
  input  [31:0] in_32,
  input  [31:0] in_33,
  output [31:0] out_34
);

  wire [31:0] mux32_1_out_4, mux32_2_out_4, mux32_3_out_4, mux32_4_out_4, mux32_5_out_4, mux32_6_out_4,
       mux32_7_out_4, mux32_8_out_4, mux32_9_out_4, mux32_10_out_4, mux32_11_out_4, mux32_12_out_4,
       mux32_13_out_4, mux32_14_out_4, mux32_15_out_4, mux32_16_out_4, mux32_17_out_4, mux32_18_out_4,
       mux32_19_out_4, mux32_20_out_4, mux32_21_out_4, mux32_22_out_4, mux32_23_out_4, mux32_24_out_4,
       mux32_25_out_4, mux32_26_out_4, mux32_27_out_4, mux32_28_out_4, mux32_29_out_4, mux32_30_out_4;

  mux32 mux32_1 (.in_3(in_3), .in_2(in_2), .in_1(in_1[0]), .out_4(mux32_1_out_4));
  mux32 mux32_2 (.in_3(in_5), .in_2(in_4), .in_1(in_1[0]), .out_4(mux32_2_out_4));
  mux32 mux32_3 (.in_3(in_7), .in_2(in_6), .in_1(in_1[0]), .out_4(mux32_3_out_4));
  mux32 mux32_4 (.in_3(in_9), .in_2(in_8), .in_1(in_1[0]), .out_4(mux32_4_out_4));
  mux32 mux32_5 (.in_3(in_11), .in_2(in_10), .in_1(in_1[0]), .out_4(mux32_5_out_4));
  mux32 mux32_6 (.in_3(in_13), .in_2(in_12), .in_1(in_1[0]), .out_4(mux32_6_out_4));
  mux32 mux32_7 (.in_3(in_15), .in_2(in_14), .in_1(in_1[0]), .out_4(mux32_7_out_4));
  mux32 mux32_8 (.in_3(in_17), .in_2(in_16), .in_1(in_1[0]), .out_4(mux32_8_out_4));
  mux32 mux32_9 (.in_3(in_19), .in_2(in_18), .in_1(in_1[0]), .out_4(mux32_9_out_4));
  mux32 mux32_10 (.in_3(in_21), .in_2(in_20), .in_1(in_1[0]), .out_4(mux32_10_out_4));
  mux32 mux32_11 (.in_3(in_23), .in_2(in_22), .in_1(in_1[0]), .out_4(mux32_11_out_4));
  mux32 mux32_12 (.in_3(in_25), .in_2(in_24), .in_1(in_1[0]), .out_4(mux32_12_out_4));
  mux32 mux32_13 (.in_3(in_27), .in_2(in_26), .in_1(in_1[0]), .out_4(mux32_13_out_4));
  mux32 mux32_14 (.in_3(in_29), .in_2(in_28), .in_1(in_1[0]), .out_4(mux32_14_out_4));
  mux32 mux32_15 (.in_3(in_31), .in_2(in_30), .in_1(in_1[0]), .out_4(mux32_15_out_4));
  mux32 mux32_16 (.in_3(in_33), .in_2(in_32), .in_1(in_1[0]), .out_4(mux32_16_out_4));
  mux32 mux32_17 (.in_3(mux32_2_out_4), .in_2(mux32_1_out_4), .in_1(in_1[1]), .out_4(mux32_17_out_4));
  mux32 mux32_18 (.in_3(mux32_4_out_4), .in_2(mux32_3_out_4), .in_1(in_1[1]), .out_4(mux32_18_out_4));
  mux32 mux32_19 (.in_3(mux32_6_out_4), .in_2(mux32_5_out_4), .in_1(in_1[1]), .out_4(mux32_19_out_4));
  mux32 mux32_20 (.in_3(mux32_8_out_4), .in_2(mux32_7_out_4), .in_1(in_1[1]), .out_4(mux32_20_out_4));
  mux32 mux32_21 (.in_3(mux32_10_out_4), .in_2(mux32_9_out_4), .in_1(in_1[1]), .out_4(mux32_21_out_4));
  mux32 mux32_22 (.in_3(mux32_12_out_4), .in_2(mux32_11_out_4), .in_1(in_1[1]), .out_4(mux32_22_out_4));
  mux32 mux32_23 (.in_3(mux32_14_out_4), .in_2(mux32_13_out_4), .in_1(in_1[1]), .out_4(mux32_23_out_4));
  mux32 mux32_24 (.in_3(mux32_16_out_4), .in_2(mux32_15_out_4), .in_1(in_1[1]), .out_4(mux32_24_out_4));
  mux32 mux32_25 (.in_3(mux32_18_out_4), .in_2(mux32_17_out_4), .in_1(in_1[2]), .out_4(mux32_25_out_4));
  mux32 mux32_26 (.in_3(mux32_20_out_4), .in_2(mux32_19_out_4), .in_1(in_1[2]), .out_4(mux32_26_out_4));
  mux32 mux32_27 (.in_3(mux32_22_out_4), .in_2(mux32_21_out_4), .in_1(in_1[2]), .out_4(mux32_27_out_4));
  mux32 mux32_28 (.in_3(mux32_24_out_4), .in_2(mux32_23_out_4), .in_1(in_1[2]), .out_4(mux32_28_out_4));
  mux32 mux32_29 (.in_3(mux32_26_out_4), .in_2(mux32_25_out_4), .in_1(in_1[3]), .out_4(mux32_29_out_4));
  mux32 mux32_30 (.in_3(mux32_28_out_4), .in_2(mux32_27_out_4), .in_1(in_1[3]), .out_4(mux32_30_out_4));
  mux32 mux32_31 (.in_3(mux32_30_out_4), .in_2(mux32_29_out_4), .in_1(in_1[4]), .out_4(out_34));
endmodule
module CPU (
  input  [31:0] read_value,
  input  [31:0] instruction,
  input  reset,
  output error,
  output [31:0] address,
  output [31:0] write_value,
  output read,
  output [31:0] pc_out,
  output [3:0] mask
);

  wire add_and_or_1_carry, and_1_out, and_2_out, and_3_out, and_4_out, and_5_out, and_6_out, and_7_out,
       and_8_out, and_9_out, and_10_out, and_11_out, and_12_out, and_13_out, and_14_out, and_15_out,
       and_16_out, and_17_out, and_18_out, and_19_out, and_20_out, and_21_out, and_22_out, and_23_out,
       and_24_out, and_25_out, and_26_out, and_27_out, and_28_out, and_29_out, and_30_out, and_31_out,
       and_32_out, and_33_out, and_34_out, and_35_out, and_36_out, and_37_out, and_38_out, and_39_out,
       and_40_out, and_41_out, and_42_out, and_43_out, and_44_out, and_45_out, and_46_out, and_47_out,
       and_48_out, and_49_out, and_50_out, and_51_out, and_52_out, and_53_out, and_54_out, and_55_out,
       and_56_out, and_57_out, and_58_out, and_59_out, and_60_out, and_61_out, and_62_out, and_63_out,
       and_64_out, and_65_out, and_66_out, and_67_out, and_68_out, and_69_out, and_70_out, and_71_out,
       and_72_out, and_73_out, and_74_out, and_75_out, and_76_out, and_77_out, and_79_out, and_80_out,
       and_81_out, and_82_out, and_83_out, and_84_out, and_85_out, and_86_out, and_87_out, and_88_out,
       and_89_out, and_90_out, and_91_out, and_92_out, and_93_out, and_94_out, and_95_out, and_96_out,
       and_97_out, and_98_out, and_99_out, and_100_out, and_101_out, and_102_out, and_103_out, and_104_out,
       and_105_out, and_106_out, and_107_out, and_108_out, and_109_out, and_110_out, and_111_out,
       and_112_out, mux_1_out_4, mux_2_out_4, mux_3_out_4, not_1_out, not_2_out, not_3_out, not_4_out,
       not_5_out, not_6_out, not_7_out, not_8_out, not_9_out, not_10_out, not_11_out, not_12_out, not_13_out,
       not_14_out, not_15_out, not_16_out, not_17_out, not_18_out, not_19_out, not_20_out, not_21_out,
       not_22_out, not_23_out, not_24_out, not_25_out, not_26_out, not_27_out, not_28_out, not_29_out,
       not_30_out, not_31_out, not_32_out, not_33_out, not_34_out, not_67_out, not_68_out, not_69_out,
       not_70_out, not_71_out, not_72_out, not_73_out, not_74_out, not_75_out, not_76_out, not_77_out,
       or_1_out, or_2_out, or_3_out, or_4_out, or_5_out, or_6_out, or_7_out, or_8_out, or_9_out, or_10_out,
       or_11_out, or_12_out, or_13_out, or_14_out, or_16_out, or_17_out, or_18_out, or_19_out, or_20_out,
       or_21_out, or_22_out, or_23_out, or_24_out, or_25_out, or_26_out, or_27_out, or_28_out, or_29_out,
       or_30_out, or_31_out, or_32_out, or_33_out, or_34_out, or_35_out, or_36_out, or_37_out, or_38_out,
       or_39_out, or_40_out, or_41_out, or_42_out, or_43_out, or_44_out, or_45_out, or_46_out, or_47_out,
       or_48_out, or_49_out, or_50_out, or_51_out, or_52_out, or_53_out, or_54_out, or_55_out, or_56_out,
       or_57_out, or_58_out, or_59_out, or_60_out, or_61_out, or_62_out, or_63_out, or_64_out, or_65_out,
       or_67_out, or_68_out, or_69_out, or_70_out, or_71_out, or_72_out, or_73_out, or_74_out, or_75_out,
       or_76_out, or_77_out, or_78_out, or_79_out, or_80_out, or_81_out, or_82_out, or_83_out, or_84_out,
       or_85_out, or_86_out, or_87_out, or_88_out, or_89_out, or_90_out, or_91_out, or_92_out, or_93_out,
       or_94_out, or_95_out, or_96_out, or_97_out, or_98_out, or_99_out, or_100_out, or_101_out, or_102_out,
       or_103_out, or_104_out, or_105_out, or_106_out, or_107_out, or_108_out, or_109_out, or_110_out,
       or_111_out, or_112_out, or_113_out, or_114_out, or_115_out, or_116_out, or_117_out, or_118_out,
       or_119_out, or_120_out, or_121_out, or_122_out, or_123_out;
  wire [4:0] mux32_15_out_4;
  wire [6:0] mux8_3_out_4, mux8_5_out_4;
  wire [7:0] mux8_1_out_4, mux8_2_out_4, mux8_4_out_4, mux8_6_out_4, mux8_7_out_4, mux8_8_out_4,
       mux8_9_out_4, mux8_10_out_4, mux8_11_out_4, mux8_12_out_4, mux8_13_out_4, mux8_14_out_4;
  wire [7:7] mux8_3_out_4_2, mux8_5_out_4_2;
  wire [15:0] mux32_26_out_4, mux32_26_out_4_2;
  wire [31:0] add_and_or_1_add_result, add_and_or_1_and_result, add_and_or_1_or_result,
       add_and_or_1_xor_result, add_er_1_result, mux32_1_out_4, mux32_2_out_4, mux32_3_out_4, mux32_4_out_4,
       mux32_5_out_4, mux32_6_out_4, mux32_7_out_4, mux32_8_out_4, mux32_9_out_4, mux32_10_out_4,
       mux32_11_out_4, mux32_12_out_4, mux32_13_out_4, mux32_14_out_4, mux32_16_out_4, mux32_17_out_4,
       mux32_18_out_4, mux32_19_out_4, mux32_20_out_4, mux32_21_out_4, mux32_22_out_4, mux32_23_out_4,
       mux32_24_out_4, mux32_25_out_4, mux32_27_out_4, mux32_28_out_4, not_35_out, pc_1_out_5,
       select_register_1_out1, select_register_1_out2;
  wire [31:5] mux32_15_out_4_2;
  wire [31:31] and_78_out;

  Clock clock_1 ();  // open: out
  not not_1 (not_1_out, error);
  not not_2 (not_2_out, and_1_out);
  and and_1 (and_1_out, instruction[0], instruction[1]);
  not not_3 (not_3_out, instruction[4]);
  not not_4 (not_4_out, instruction[5]);
  not not_5 (not_5_out, instruction[6]);
  not not_6 (not_6_out, instruction[4]);
  not not_7 (not_7_out, instruction[6]);
  not not_8 (not_8_out, instruction[6]);
  not not_9 (not_9_out, instruction[5]);
  not not_10 (not_10_out, instruction[6]);
  not not_11 (not_11_out, instruction[4]);
  not not_12 (not_12_out, instruction[3]);
  not not_13 (not_13_out, instruction[2]);
  not not_14 (not_14_out, instruction[3]);
  and and_2 (and_2_out, not_12_out, not_13_out);
  and and_3 (and_3_out, not_14_out, instruction[2]);
  and and_4 (and_4_out, not_3_out, not_4_out);
  and and_5 (and_5_out, and_4_out, not_5_out);
  and and_6 (and_6_out, not_6_out, instruction[5]);
  and and_7 (and_7_out, and_6_out, not_7_out);
  and and_8 (and_8_out, instruction[4], instruction[5]);
  and and_9 (and_9_out, and_8_out, not_8_out);
  and and_10 (and_10_out, instruction[4], not_9_out);
  and and_11 (and_11_out, and_10_out, not_10_out);
  and and_12 (and_12_out, not_11_out, instruction[5]);
  and and_13 (and_13_out, and_12_out, instruction[6]);
  and and_14 (and_14_out, instruction[4], instruction[5]);
  and and_15 (and_15_out, and_14_out, instruction[6]);
  and and_16 (and_16_out, instruction[3], instruction[2]);
  and and_17 (and_17_out, and_5_out, and_2_out);
  and and_18 (and_18_out, and_7_out, and_2_out);
  and and_19 (and_19_out, and_9_out, and_2_out);
  and and_20 (and_20_out, and_11_out, and_2_out);
  and and_21 (and_21_out, and_13_out, and_2_out);
  and and_22 (and_22_out, and_2_out, and_15_out);
  and and_23 (and_23_out, and_9_out, and_3_out);
  and and_24 (and_24_out, and_11_out, and_3_out);
  and and_25 (and_25_out, and_16_out, and_13_out);
  and and_26 (and_26_out, and_3_out, and_13_out);
  and and_27 (and_27_out, and_16_out, and_5_out);
  or or_1 (or_1_out, and_17_out, and_18_out);
  or or_2 (or_2_out, or_1_out, or_3_out);
  or or_3 (or_3_out, and_19_out, and_20_out);
  or or_4 (or_4_out, and_21_out, and_23_out);
  or or_5 (or_5_out, or_4_out, or_8_out);
  or or_6 (or_6_out, or_2_out, or_5_out);
  mux8 mux8_1 (.in_1(or_13_out), .in_3(read_value[15:8]), .in_2(read_value[7:0]), .out_4(mux8_1_out_4));
  mux8 mux8_2 (.in_1(or_13_out), .in_3(read_value[31:24]), .in_2(read_value[23:16]), .out_4(mux8_2_out_4));
  and and_28 (and_28_out, mask[3], mask[2]);
  and and_29 (and_29_out, mask[1], mask[0]);
  not not_15 (not_15_out, mask[0]);
  not not_16 (not_16_out, mask[1]);
  not not_17 (not_17_out, mask[2]);
  not not_18 (not_18_out, mask[3]);
  or or_7 (or_7_out, not_2_out, not_19_out);
  or or_8 (or_8_out, and_24_out, and_25_out);
  or or_9 (or_9_out, and_26_out, and_27_out);
  or or_10 (or_10_out, or_9_out, and_22_out);
  or or_11 (or_11_out, or_6_out, or_10_out);
  not not_19 (not_19_out, or_11_out);
  mux8 mux8_3 (.in_1(or_12_out), .in_3(mux8_2_out_4), .in_2(mux8_1_out_4), .out_4({mux8_3_out_4_2[7], mux8_3_out_4}));
  and and_30 (and_30_out, and_28_out, and_29_out);
  or or_12 (or_12_out, mask[2], mask[3]);
  or or_13 (or_13_out, mask[1], mask[3]);
  and and_31 (and_31_out, and_28_out, and_32_out);
  and and_32 (and_32_out, not_15_out, not_16_out);
  and and_33 (and_33_out, not_17_out, not_18_out);
  and and_34 (and_34_out, and_33_out, and_29_out);
  not not_20 (not_20_out, or_7_out);
  and and_35 (and_35_out, not_20_out, and_17_out);
  and and_36 (and_36_out, not_20_out, and_18_out);
  and and_37 (and_37_out, not_20_out, and_19_out);
  and and_38 (and_38_out, not_20_out, and_20_out);
  and and_39 (and_39_out, not_20_out, and_21_out);
  and and_40 (and_40_out, not_20_out, and_23_out);
  and and_41 (and_41_out, not_20_out, and_24_out);
  and and_42 (and_42_out, not_20_out, and_25_out);
  and and_43 (and_43_out, not_20_out, and_26_out);
  and and_44 (and_44_out, not_20_out, and_27_out);
  and and_45 (and_45_out, not_20_out, and_22_out);
  mux32 mux32_1 (
    .in_3({{21{instruction[31]}}, instruction[30:20]}), .in_2({32{1'b0}}), .in_1(or_21_out),
    .out_4(mux32_1_out_4));
  mux8 mux8_4 (.in_1(and_31_out), .in_3(read_value[23:16]), .in_2(read_value[7:0]), .out_4(mux8_4_out_4));
  mux8 mux8_5 (
    .in_1(and_31_out), .in_3(read_value[31:24]), .in_2(read_value[15:8]),
    .out_4({mux8_5_out_4_2[7], mux8_5_out_4}));
  or or_14 (or_14_out, and_31_out, and_34_out);
  mux32 mux32_2 (
    .in_3({{21{instruction[31]}}, instruction[30:25], instruction[11:7]}), .in_2(mux32_1_out_4),
    .in_1(and_36_out), .out_4(mux32_2_out_4));
  mux8 mux8_6 (.in_1(or_14_out), .in_3(mux8_4_out_4), .in_2({mux8_3_out_4_2[7], mux8_3_out_4}), .out_4(mux8_6_out_4));
  mux8 mux8_7 (.in_1(or_14_out), .in_3({mux8_5_out_4_2[7], mux8_5_out_4}), .in_2(mux8_12_out_4), .out_4(mux8_7_out_4));
  mux32 mux32_3 (
    .in_3({{20{instruction[31]}}, instruction[7], instruction[30:25], instruction[11:8], 1'b0}),
    .in_2(mux32_2_out_4), .in_1(and_39_out), .out_4(mux32_3_out_4));
  mux32 mux32_4 (
    .in_3({instruction[31:12], {12{1'b0}}}), .in_2(mux32_3_out_4), .in_1(or_22_out), .out_4(mux32_4_out_4));
  mux8 mux8_8 (.in_1(and_30_out), .in_3(read_value[7:0]), .in_2(mux8_6_out_4), .out_4(mux8_8_out_4));
  mux8 mux8_9 (.in_1(and_30_out), .in_3(read_value[15:8]), .in_2(mux8_7_out_4), .out_4(mux8_9_out_4));
  mux8 mux8_10 (.in_1(and_30_out), .in_3(read_value[23:16]), .in_2(mux8_14_out_4), .out_4(mux8_10_out_4));
  mux8 mux8_11 (.in_1(and_30_out), .in_3(read_value[31:24]), .in_2(mux8_14_out_4), .out_4(mux8_11_out_4));
  mux8 mux8_12 (.in_1(and_94_out), .in_3({8{1'b0}}), .in_2({8{mux8_3_out_4_2[7]}}), .out_4(mux8_12_out_4));
  mux8 mux8_13 (.in_1(and_94_out), .in_3({8{1'b0}}), .in_2({8{mux8_5_out_4_2[7]}}), .out_4(mux8_13_out_4));
  or or_15 (error, or_16_out, and_46_out);
  or or_16 (or_16_out, or_7_out, not_33_out);
  mux32 mux32_5 (
    .in_3({{12{instruction[31]}}, instruction[19:12], instruction[20], instruction[30:21], 1'b0}),
    .in_2(mux32_4_out_4), .in_1(and_42_out), .out_4(mux32_5_out_4));
  mux8 mux8_14 (.in_1(or_14_out), .in_3(mux8_13_out_4), .in_2(mux8_12_out_4), .out_4(mux8_14_out_4));
  and and_46 (and_46_out, and_98_out, or_17_out);
  or or_17 (or_17_out, and_35_out, and_36_out);
  not not_21 (not_21_out, and_36_out);
  or or_18 (or_18_out, and_45_out, and_44_out);
  or or_19 (or_19_out, and_43_out, and_38_out);
  or or_20 (or_20_out, or_18_out, or_19_out);
  or or_21 (or_21_out, or_20_out, and_35_out);
  not not_22 (not_22_out, or_17_out);
  and and_47 (and_47_out, and_35_out, not_21_out);
  or or_22 (or_22_out, and_41_out, and_40_out);
  and and_48 (and_48_out, not_1_out, not_23_out);
  or or_23 (or_23_out, and_37_out, and_39_out);
  or or_24 (or_24_out, and_42_out, and_41_out);
  mux32 mux32_6 (
    .in_3(add_er_1_result), .in_2({mux32_26_out_4_2, mux32_26_out_4}), .in_1(and_42_out),
    .out_4(mux32_6_out_4));
  and and_49 (and_49_out, and_39_out, mux_2_out_4);
  mux32 mux32_7 (
    .in_3({mux32_26_out_4_2, mux32_26_out_4}), .in_2(add_er_1_result), .in_1(and_43_out),
    .out_4(mux32_7_out_4));
  not not_23 (not_23_out, or_29_out);
  and and_50 (and_50_out, not_1_out, or_29_out);
  pc pc_1 (.load(and_50_out), .reset(reset), .inc(and_48_out), .in_4(mux32_7_out_4), .out_5(pc_1_out_5));
  or or_25 (or_25_out, and_35_out, and_37_out);
  or or_26 (or_26_out, and_38_out, and_40_out);
  or or_27 (or_27_out, or_25_out, or_26_out);
  or or_28 (or_28_out, or_27_out, or_32_out);
  mux32 mux32_8 (
    .in_3({mux8_11_out_4, mux8_10_out_4, mux8_9_out_4, mux8_8_out_4}), .in_2(mux32_6_out_4),
    .in_1(and_35_out), .out_4(mux32_8_out_4));
  or or_29 (or_29_out, and_49_out, or_30_out);
  mux32 mux32_9 (
    .in_3(mux32_14_out_4),
    .in_2({mux32_14_out_4[0], mux32_14_out_4[1], mux32_14_out_4[2], mux32_14_out_4[3], mux32_14_out_4[4], mux32_14_out_4[5], mux32_14_out_4[6], mux32_14_out_4[7], mux32_14_out_4[8], mux32_14_out_4[9], mux32_14_out_4[10], mux32_14_out_4[11], mux32_14_out_4[12], mux32_14_out_4[13], mux32_14_out_4[14], mux32_14_out_4[15], mux32_14_out_4[16], mux32_14_out_4[17], mux32_14_out_4[18], mux32_14_out_4[19], mux32_14_out_4[20], mux32_14_out_4[21], mux32_14_out_4[22], mux32_14_out_4[23], mux32_14_out_4[24], mux32_14_out_4[25], mux32_14_out_4[26], mux32_14_out_4[27], mux32_14_out_4[28], mux32_14_out_4[29], mux32_14_out_4[30], mux32_14_out_4[31]}),
    .in_1(or_82_out), .out_4(mux32_9_out_4));
  or or_30 (or_30_out, and_43_out, and_42_out);
  or or_31 (or_31_out, and_37_out, and_36_out);
  or or_32 (or_32_out, or_30_out, and_41_out);
  or or_33 (or_33_out, or_31_out, or_35_out);
  or or_34 (or_34_out, and_39_out, or_31_out);
  or or_35 (or_35_out, and_35_out, and_43_out);
  or or_36 (or_36_out, and_38_out, and_39_out);
  or or_37 (or_37_out, or_33_out, or_36_out);
  select_register select_register_1 (
    .load2(or_34_out), .store(or_28_out), .load1(or_37_out), .rs2(instruction[24:20]),
    .rd(instruction[11:7]), .rs1(instruction[19:15]), .in1(mux32_8_out_4), .out1(select_register_1_out1),
    .out2(select_register_1_out2));
  mux32 mux32_10 (
    .in_3({and_78_out[31], mux32_9_out_4[31:1]}), .in_2(mux32_9_out_4), .in_1(mux32_15_out_4[0]),
    .out_4(mux32_10_out_4));
  mux32 mux32_11 (.in_3(pc_1_out_5), .in_2(select_register_1_out1), .in_1(or_24_out), .out_4(mux32_11_out_4));
  mux32 mux32_12 (.in_3(select_register_1_out2), .in_2(mux32_5_out_4), .in_1(or_23_out), .out_4(mux32_12_out_4));
  mux32 mux32_13 (
    .in_3({{2{and_78_out[31]}}, mux32_10_out_4[31:2]}), .in_2(mux32_10_out_4), .in_1(mux32_15_out_4[1]),
    .out_4(mux32_13_out_4));
  mux32 mux32_14 (
    .in_3({32{1'b0}}), .in_2(mux32_11_out_4), .in_1(and_40_out),
    .out_4({mux32_14_out_4[0], mux32_14_out_4[1], mux32_14_out_4[2], mux32_14_out_4[3], mux32_14_out_4[4], mux32_14_out_4[5], mux32_14_out_4[6], mux32_14_out_4[7], mux32_14_out_4[8], mux32_14_out_4[9], mux32_14_out_4[10], mux32_14_out_4[11], mux32_14_out_4[12], mux32_14_out_4[13], mux32_14_out_4[14], mux32_14_out_4[15], mux32_14_out_4[16], mux32_14_out_4[17], mux32_14_out_4[18], mux32_14_out_4[19], mux32_14_out_4[20], mux32_14_out_4[21], mux32_14_out_4[22], mux32_14_out_4[23], mux32_14_out_4[24], mux32_14_out_4[25], mux32_14_out_4[26], mux32_14_out_4[27], mux32_14_out_4[28], mux32_14_out_4[29], mux32_14_out_4[30], mux32_14_out_4[31]}));
  mux32 mux32_15 (.in_3(32'h4), .in_2(mux32_12_out_4), .in_1(and_42_out), .out_4({mux32_15_out_4_2, mux32_15_out_4}));
  mux32 mux32_16 (.in_3(32'h4), .in_2(mux32_5_out_4), .in_1(and_43_out), .out_4(mux32_16_out_4));
  mux32 mux32_17 (
    .in_3({{4{and_78_out[31]}}, mux32_13_out_4[31:4]}), .in_2(mux32_13_out_4), .in_1(mux32_15_out_4[2]),
    .out_4(mux32_17_out_4));
  not not_24 (not_24_out, instruction[30]);
  or or_38 (or_38_out, or_39_out, or_40_out);
  or or_39 (or_39_out, or_41_out, and_55_out);
  or or_40 (or_40_out, and_74_out, and_93_out);
  or or_41 (or_41_out, and_51_out, and_54_out);
  and and_51 (and_51_out, and_76_out, not_25_out);
  not not_25 (not_25_out, instruction[14]);
  add_er add_er_1 (.A(pc_1_out_5), .B(mux32_16_out_4), .result(add_er_1_result));
  mux32 mux32_18 (
    .in_3({{8{and_78_out[31]}}, mux32_17_out_4[31:8]}), .in_2(mux32_17_out_4), .in_1(mux32_15_out_4[3]),
    .out_4(mux32_18_out_4));
  and and_52 (and_52_out, or_38_out, and_35_out);
  and and_53 (and_53_out, or_39_out, and_36_out);
  and and_54 (and_54_out, and_94_out, not_26_out);
  and and_55 (and_55_out, and_97_out, not_27_out);
  not not_26 (not_26_out, instruction[14]);
  not not_27 (not_27_out, instruction[14]);
  mux mux_1 (.in_2(mux32_26_out_4_2[15]), .in_3(not_68_out), .in_1(and_76_out), .out_4(mux_1_out_4));
  not not_28 (not_28_out, mux_1_out_4);
  and and_56 (and_56_out, and_37_out, and_51_out);
  and and_57 (and_57_out, and_37_out, and_54_out);
  and and_58 (and_58_out, and_37_out, and_55_out);
  and and_59 (and_59_out, and_37_out, and_75_out);
  and and_60 (and_60_out, and_37_out, and_74_out);
  and and_61 (and_61_out, and_37_out, and_93_out);
  and and_62 (and_62_out, and_37_out, and_96_out);
  and and_63 (and_63_out, and_37_out, and_100_out);
  and and_64 (and_64_out, and_38_out, and_51_out);
  and and_65 (and_65_out, and_38_out, and_54_out);
  and and_66 (and_66_out, and_38_out, and_55_out);
  and and_67 (and_67_out, and_38_out, and_75_out);
  and and_68 (and_68_out, and_38_out, and_74_out);
  and and_69 (and_69_out, and_38_out, and_93_out);
  and and_70 (and_70_out, and_38_out, and_96_out);
  and and_71 (and_71_out, and_38_out, and_96_out);
  and and_72 (and_72_out, and_39_out, or_46_out);
  and and_73 (and_73_out, and_39_out, or_44_out);
  or or_42 (or_42_out, and_41_out, and_42_out);
  or or_43 (or_43_out, and_44_out, and_45_out);
  or or_44 (or_44_out, and_100_out, and_96_out);
  or or_45 (or_45_out, and_51_out, and_54_out);
  or or_46 (or_46_out, or_45_out, or_47_out);
  or or_47 (or_47_out, and_74_out, and_93_out);
  and and_74 (and_74_out, and_76_out, instruction[14]);
  and and_75 (and_75_out, and_98_out, not_29_out);
  and and_76 (and_76_out, not_30_out, not_31_out);
  not not_29 (not_29_out, instruction[14]);
  not not_30 (not_30_out, instruction[12]);
  not not_31 (not_31_out, instruction[13]);
  mux mux_2 (.in_2(mux_1_out_4), .in_3(not_28_out), .in_1(and_94_out), .out_4(mux_2_out_4));
  and and_77 (and_77_out, or_83_out, or_82_out);
  and and_78 (and_78_out[31], mux32_14_out_4[0], and_77_out);
  mux32 mux32_19 (
    .in_3({{16{and_78_out[31]}}, mux32_18_out_4[31:16]}), .in_2(mux32_18_out_4), .in_1(mux32_15_out_4[4]),
    .out_4(mux32_19_out_4));
  and and_79 (and_79_out, not_24_out, and_56_out);
  and and_80 (and_80_out, and_56_out, instruction[30]);
  and and_81 (and_81_out, not_24_out, and_57_out);
  and and_82 (and_82_out, not_24_out, and_58_out);
  and and_83 (and_83_out, not_24_out, and_59_out);
  and and_84 (and_84_out, not_24_out, and_60_out);
  and and_85 (and_85_out, not_24_out, and_61_out);
  and and_86 (and_86_out, and_61_out, instruction[30]);
  and and_87 (and_87_out, and_62_out, not_24_out);
  and and_88 (and_88_out, and_63_out, not_24_out);
  and and_89 (and_89_out, and_65_out, instruction[30]);
  and and_90 (and_90_out, not_24_out, and_69_out);
  and and_91 (and_91_out, and_69_out, instruction[30]);
  or or_48 (or_48_out, and_43_out, and_92_out);
  and and_92 (and_92_out, not_24_out, or_43_out);
  and and_93 (and_93_out, and_94_out, instruction[14]);
  and and_94 (and_94_out, instruction[12], not_32_out);
  not not_32 (not_32_out, instruction[13]);
  mux32 mux32_20 (
    .in_3({mux32_19_out_4[0], mux32_19_out_4[1], mux32_19_out_4[2], mux32_19_out_4[3], mux32_19_out_4[4], mux32_19_out_4[5], mux32_19_out_4[6], mux32_19_out_4[7], mux32_19_out_4[8], mux32_19_out_4[9], mux32_19_out_4[10], mux32_19_out_4[11], mux32_19_out_4[12], mux32_19_out_4[13], mux32_19_out_4[14], mux32_19_out_4[15], mux32_19_out_4[16], mux32_19_out_4[17], mux32_19_out_4[18], mux32_19_out_4[19], mux32_19_out_4[20], mux32_19_out_4[21], mux32_19_out_4[22], mux32_19_out_4[23], mux32_19_out_4[24], mux32_19_out_4[25], mux32_19_out_4[26], mux32_19_out_4[27], mux32_19_out_4[28], mux32_19_out_4[29], mux32_19_out_4[30], mux32_19_out_4[31]}),
    .in_2(mux32_19_out_4), .in_1(or_82_out), .out_4(mux32_20_out_4));
  not not_33 (not_33_out, or_69_out);
  or or_49 (or_49_out, or_42_out, and_52_out);
  or or_50 (or_50_out, or_49_out, and_53_out);
  or or_51 (or_51_out, and_79_out, or_52_out);
  or or_52 (or_52_out, and_64_out, and_95_out);
  or or_53 (or_53_out, and_88_out, and_71_out);
  or or_54 (or_54_out, and_87_out, and_70_out);
  or or_55 (or_55_out, and_81_out, and_66_out);
  or or_56 (or_56_out, and_85_out, and_67_out);
  or or_57 (or_57_out, and_86_out, and_89_out);
  or or_58 (or_58_out, and_90_out, and_82_out);
  or or_59 (or_59_out, and_83_out, and_91_out);
  or or_60 (or_60_out, and_40_out, or_65_out);
  and and_95 (and_95_out, and_51_out, or_48_out);
  and and_96 (and_96_out, and_97_out, instruction[14]);
  and and_97 (and_97_out, not_34_out, instruction[13]);
  and and_98 (and_98_out, instruction[12], instruction[13]);
  not not_34 (not_34_out, instruction[12]);
  and and_99 (and_99_out, or_77_out, or_79_out);
  or or_61 (or_61_out, and_99_out, or_82_out);
  not not_35 (not_35_out[0], mux32_15_out_4[0]);
  not not_36 (not_35_out[1], mux32_15_out_4[1]);
  not not_37 (not_35_out[2], mux32_15_out_4[2]);
  not not_38 (not_35_out[3], mux32_15_out_4[3]);
  not not_39 (not_35_out[4], mux32_15_out_4[4]);
  not not_40 (not_35_out[5], mux32_15_out_4_2[5]);
  not not_41 (not_35_out[6], mux32_15_out_4_2[6]);
  not not_42 (not_35_out[7], mux32_15_out_4_2[7]);
  not not_43 (not_35_out[8], mux32_15_out_4_2[8]);
  not not_44 (not_35_out[9], mux32_15_out_4_2[9]);
  not not_45 (not_35_out[10], mux32_15_out_4_2[10]);
  not not_46 (not_35_out[11], mux32_15_out_4_2[11]);
  not not_47 (not_35_out[12], mux32_15_out_4_2[12]);
  not not_48 (not_35_out[13], mux32_15_out_4_2[13]);
  not not_49 (not_35_out[14], mux32_15_out_4_2[14]);
  not not_50 (not_35_out[15], mux32_15_out_4_2[15]);
  not not_51 (not_35_out[16], mux32_15_out_4_2[16]);
  not not_52 (not_35_out[17], mux32_15_out_4_2[17]);
  not not_53 (not_35_out[18], mux32_15_out_4_2[18]);
  not not_54 (not_35_out[19], mux32_15_out_4_2[19]);
  not not_55 (not_35_out[20], mux32_15_out_4_2[20]);
  not not_56 (not_35_out[21], mux32_15_out_4_2[21]);
  not not_57 (not_35_out[22], mux32_15_out_4_2[22]);
  not not_58 (not_35_out[23], mux32_15_out_4_2[23]);
  not not_59 (not_35_out[24], mux32_15_out_4_2[24]);
  not not_60 (not_35_out[25], mux32_15_out_4_2[25]);
  not not_61 (not_35_out[26], mux32_15_out_4_2[26]);
  not not_62 (not_35_out[27], mux32_15_out_4_2[27]);
  not not_63 (not_35_out[28], mux32_15_out_4_2[28]);
  not not_64 (not_35_out[29], mux32_15_out_4_2[29]);
  not not_65 (not_35_out[30], mux32_15_out_4_2[30]);
  not not_66 (not_35_out[31], mux32_15_out_4_2[31]);
  or or_62 (or_62_out, or_63_out, and_80_out);
  or or_63 (or_63_out, or_50_out, or_51_out);
  or or_64 (or_64_out, or_53_out, or_54_out);
  or or_65 (or_65_out, and_84_out, and_68_out);
  or or_66 (or_60_out, or_55_out, or_56_out);
  or or_67 (or_67_out, or_58_out, and_72_out);
  or or_68 (or_68_out, or_59_out, and_73_out);
  and and_100 (and_100_out, and_98_out, instruction[14]);
  mux32 mux32_21 (
    .in_3(not_35_out), .in_2({mux32_15_out_4_2, mux32_15_out_4}), .in_1(or_61_out), .out_4(mux32_21_out_4));
  not not_67 (not_67_out, add_and_or_1_carry);
  or or_69 (or_69_out, or_62_out, or_70_out);
  or or_70 (or_70_out, or_64_out, or_71_out);
  or or_71 (or_71_out, or_72_out, or_74_out);
  or or_72 (or_72_out, or_60_out, or_60_out);
  or or_73 (or_73_out, or_54_out, and_40_out);
  add_and_or add_and_or_1 (
    .b(mux32_21_out_4),
    .a({mux32_14_out_4[0], mux32_14_out_4[1], mux32_14_out_4[2], mux32_14_out_4[3], mux32_14_out_4[4], mux32_14_out_4[5], mux32_14_out_4[6], mux32_14_out_4[7], mux32_14_out_4[8], mux32_14_out_4[9], mux32_14_out_4[10], mux32_14_out_4[11], mux32_14_out_4[12], mux32_14_out_4[13], mux32_14_out_4[14], mux32_14_out_4[15], mux32_14_out_4[16], mux32_14_out_4[17], mux32_14_out_4[18], mux32_14_out_4[19], mux32_14_out_4[20], mux32_14_out_4[21], mux32_14_out_4[22], mux32_14_out_4[23], mux32_14_out_4[24], mux32_14_out_4[25], mux32_14_out_4[26], mux32_14_out_4[27], mux32_14_out_4[28], mux32_14_out_4[29], mux32_14_out_4[30], mux32_14_out_4[31]}),
    .neg(or_61_out), .xor_result(add_and_or_1_xor_result), .add_result(add_and_or_1_add_result),
    .and_result(add_and_or_1_and_result), .or_result(add_and_or_1_or_result), .carry(add_and_or_1_carry));
  mux mux_3 (.in_2(add_and_or_1_add_result[31]), .in_3(not_67_out), .in_1(or_83_out), .out_4(mux_3_out_4));
  or or_74 (or_74_out, or_57_out, or_75_out);
  or or_75 (or_75_out, or_67_out, or_68_out);
  or or_76 (or_76_out, or_60_out, or_57_out);
  or or_77 (or_77_out, or_76_out, or_75_out);
  or or_78 (or_78_out, or_64_out, or_65_out);
  or or_79 (or_79_out, or_78_out, or_80_out);
  or or_80 (or_80_out, or_75_out, and_40_out);
  or or_81 (or_81_out, and_80_out, or_57_out);
  or or_82 (or_82_out, or_81_out, or_56_out);
  or or_83 (or_83_out, or_68_out, or_57_out);
  mux32 mux32_22 (.in_3(mux32_27_out_4), .in_2(add_and_or_1_add_result), .in_1(or_77_out), .out_4(mux32_22_out_4));
  mux32 mux32_23 (
    .in_3(add_and_or_1_or_result), .in_2(add_and_or_1_and_result), .in_1(or_60_out), .out_4(mux32_23_out_4));
  mux32 mux32_24 (
    .in_3({mux32_15_out_4_2, mux32_15_out_4}), .in_2(add_and_or_1_xor_result), .in_1(or_60_out),
    .out_4(mux32_24_out_4));
  mux32 mux32_25 (.in_3(32'h1), .in_2({32{1'b0}}), .in_1(mux_3_out_4), .out_4(mux32_25_out_4));
  mux32 mux32_26 (
    .in_3(mux32_28_out_4), .in_2(mux32_22_out_4), .in_1(or_79_out), .out_4({mux32_26_out_4_2, mux32_26_out_4}));
  mux32 mux32_27 (.in_3(mux32_24_out_4), .in_2(mux32_23_out_4), .in_1(or_73_out), .out_4(mux32_27_out_4));
  mux32 mux32_28 (.in_3(mux32_25_out_4), .in_2(mux32_20_out_4), .in_1(or_77_out), .out_4(mux32_28_out_4));
  or or_84 (or_84_out, mux32_26_out_4[0], mux32_26_out_4[1]);
  or or_85 (or_85_out, mux32_26_out_4[2], mux32_26_out_4[3]);
  or or_86 (or_86_out, mux32_26_out_4[4], mux32_26_out_4[5]);
  or or_87 (or_87_out, mux32_26_out_4[6], mux32_26_out_4[7]);
  or or_88 (or_88_out, mux32_26_out_4[8], mux32_26_out_4[9]);
  or or_89 (or_89_out, mux32_26_out_4[10], mux32_26_out_4[11]);
  or or_90 (or_90_out, mux32_26_out_4[12], mux32_26_out_4[13]);
  or or_91 (or_91_out, mux32_26_out_4[14], mux32_26_out_4[15]);
  or or_92 (or_92_out, mux32_26_out_4_2[0], mux32_26_out_4_2[1]);
  or or_93 (or_93_out, mux32_26_out_4_2[2], mux32_26_out_4_2[3]);
  or or_94 (or_94_out, mux32_26_out_4_2[4], mux32_26_out_4_2[5]);
  or or_95 (or_95_out, mux32_26_out_4_2[6], mux32_26_out_4_2[7]);
  or or_96 (or_96_out, mux32_26_out_4_2[8], mux32_26_out_4_2[9]);
  or or_97 (or_97_out, mux32_26_out_4_2[10], mux32_26_out_4_2[11]);
  or or_98 (or_98_out, mux32_26_out_4_2[12], mux32_26_out_4_2[13]);
  or or_99 (or_99_out, mux32_26_out_4_2[14], mux32_26_out_4_2[15]);
  or or_100 (or_100_out, or_84_out, or_85_out);
  or or_101 (or_101_out, or_100_out, or_102_out);
  or or_102 (or_102_out, or_86_out, or_87_out);
  or or_103 (or_103_out, or_101_out, or_105_out);
  or or_104 (or_104_out, or_88_out, or_89_out);
  or or_105 (or_105_out, or_104_out, or_106_out);
  or or_106 (or_106_out, or_90_out, or_91_out);
  or or_107 (or_107_out, or_103_out, or_111_out);
  not not_68 (not_68_out, or_107_out);
  or or_108 (or_108_out, or_92_out, or_93_out);
  or or_109 (or_109_out, or_108_out, or_110_out);
  or or_110 (or_110_out, or_94_out, or_95_out);
  or or_111 (or_111_out, or_109_out, or_113_out);
  or or_112 (or_112_out, or_96_out, or_97_out);
  or or_113 (or_113_out, or_112_out, or_114_out);
  or or_114 (or_114_out, or_98_out, or_99_out);
  not not_69 (not_69_out, mux32_26_out_4[1]);
  and and_101 (and_101_out, not_72_out, not_73_out);
  and and_102 (and_102_out, mux32_26_out_4[0], not_74_out);
  and and_103 (and_103_out, not_75_out, mux32_26_out_4[1]);
  and and_104 (and_104_out, mux32_26_out_4[0], mux32_26_out_4[1]);
  and and_105 (and_105_out, and_101_out, and_76_out);
  and and_106 (and_106_out, not_69_out, and_94_out);
  and and_107 (and_107_out, and_102_out, and_76_out);
  and and_108 (and_108_out, not_69_out, and_94_out);
  and and_109 (and_109_out, and_103_out, and_76_out);
  not not_70 (not_70_out, not_69_out);
  and and_110 (and_110_out, not_70_out, and_94_out);
  and and_111 (and_111_out, and_104_out, and_76_out);
  not not_71 (not_71_out, not_69_out);
  and and_112 (and_112_out, not_71_out, and_94_out);
  not not_72 (not_72_out, mux32_26_out_4[0]);
  not not_73 (not_73_out, mux32_26_out_4[1]);
  not not_74 (not_74_out, mux32_26_out_4[1]);
  not not_75 (not_75_out, mux32_26_out_4[0]);
  or or_115 (or_115_out, and_105_out, and_106_out);
  or or_116 (or_116_out, and_107_out, and_108_out);
  or or_117 (or_117_out, and_109_out, and_110_out);
  or or_118 (or_118_out, and_111_out, and_112_out);
  not not_76 (not_76_out, or_123_out);
  or or_119 (or_119_out, or_115_out, and_97_out);
  or or_120 (or_120_out, or_116_out, and_97_out);
  or or_121 (or_121_out, or_117_out, and_97_out);
  or or_122 (or_122_out, or_118_out, and_97_out);
  or or_123 (or_123_out, error, not_22_out);
  and and_113 (mask[0], not_76_out, or_119_out);
  and and_114 (mask[1], not_76_out, or_120_out);
  and and_115 (mask[2], not_76_out, or_121_out);
  and and_116 (mask[3], not_76_out, or_122_out);
  mux32 mux32_29 (.in_3({32{1'b0}}), .in_2({mux32_26_out_4_2, mux32_26_out_4}), .in_1(or_123_out), .out_4(address));
  mux32 mux32_30 (.in_3({32{1'b0}}), .in_2(select_register_1_out2), .in_1(or_123_out), .out_4(write_value));
  not not_77 (not_77_out, error);
  and and_117 (read, not_77_out, and_47_out);
  mux32 mux32_31 (.in_3({32{1'b0}}), .in_2(pc_1_out_5), .in_1(error), .out_4(pc_out));

  // Notes on the sheet:
  //   input
  //   output
endmodule
